// Logisim project SOBOL.circ as structural Verilog: 11 circuits, main circuit main
module main (
  input  [7:0] IN_OUT,
  output Reset_pin,
  output [7:0] out_3
);

  wire adder_4_cout, addmod_1_carryout, addmod_1_halfcarryout, addmod_1_isazero, addmod_1_negative,
       addmod_1_signcarry, buffer_1_out, comparator_1_eq, comparator_1_gt, CONTINUE_out,
       controlled_buffer_1_out, controlled_buffer_2_out, controlled_buffer_77_out, controlled_buffer_78_out,
       controlled_buffer_79_out, controlled_buffer_80_out, controlled_buffer_83_out,
       controlled_buffer_84_out, controlled_buffer_85_out, controlled_buffer_86_out, counter_1_carry,
       decoder_1_out0, decoder_1_out1, decoder_1_out2, decoder_1_out3, decoder_1_out4, decoder_1_out5,
       decoder_1_out6, decoder_1_out7, equals_1_res, equals_2_res, equals_3_res, equals_4_res, equals_5_res,
       equals_6_res, equals_7_res, equals_8_res, equals_9_res, equals_10_res, equals_11_res, equals_12_res,
       equals_13_res, equals_14_res, equals_15_res, equals_16_res, equals_17_res, equals_18_res,
       equals_19_res, equals_20_res, equals_21_res, equals_22_res, equals_23_res, equals_24_res,
       equals_25_res, equals_26_res, equals_27_res, equals_28_res, equals_29_res, equals_30_res,
       equals_31_res, equals_32_res, equals_33_res, equals_34_res, equals_35_res, equals_36_res,
       equals_37_res, equals_38_res, equals_39_res, equals_40_res, equals_41_res, equals_42_res,
       equals_43_res, equals_44_res, equals_45_res, equals_46_res, equals_47_res, equals_48_res,
       equals_49_res, equals_50_res, equals_51_res, equals_52_res, equals_53_res, equals_54_res,
       equals_55_res, equals_56_res, equals_57_res, equals_58_res, equals_59_res, equals_60_res,
       equals_61_res, equals_62_res, equals_63_res, equals_64_res, equals_65_res, equals_66_res,
       equals_67_res, equals_68_res, equals_69_res, equals_70_res, equals_71_res, equals_72_res,
       equals_73_res, equals_74_res, equals_75_res, equals_76_res, equals_77_res, equals_78_res,
       equals_79_res, equals_80_res, equals_81_res, equals_82_res, equals_83_res, equals_84_res,
       equals_85_res, equals_86_res, equals_87_res, equals_88_res, equals_89_res, equals_90_res,
       equals_91_res, equals_92_res, equals_93_res, equals_94_res, equals_95_res, equals_96_res,
       equals_97_res, equals_98_res, equals_99_res, equals_100_res, equals_101_res, equals_102_res,
       equals_103_res, equals_104_res, equals_105_res, equals_106_res, equals_107_res, equals_108_res,
       equals_109_res, equals_110_res, equals_111_res, equals_112_res, equals_113_res, equals_114_res,
       equals_115_res, equals_116_res, equals_117_res, equals_118_res, equals_119_res, equals_120_res,
       equals_121_res, equals_122_res, equals_123_res, equals_124_res, equals_125_res, equals_126_res,
       equals_127_res, equals_128_res, equals_129_res, equals_130_res, equals_151_res, equals_152_res,
       equals_153_res, equals_154_res, equals_156_res, equals_157_res, equals_158_res, equals_159_res,
       equals_160_res, equals_161_res, equals_162_res, equals_163_res, equals_164_res, equals_165_res,
       equals_166_res, equals_167_res, equals_168_res, equals_169_res, equals_170_res, equals_171_res,
       HALT_out, iszero_1_out_2, iszero_2_out_2, iszero_3_out_2, iszero_4_out_2, iszero_5_out_2,
       iszero_6_out_2, iszero_7_out_2, Main_clock_out, multiplexer_12_out, nand_1_out, nctotf_1_res,
       nctotf_2_res, nctotf_3_res, nctotf_4_res, nctotf_5_res, nctotf_6_res, nctotf_7_res, nctotf_8_res,
       nctotf_9_res, nctotf_10_res, nctotf_11_res, nctotf_12_res, nctotf_13_res, nctotf_14_res,
       nctotf_15_res, nctotf_16_res, nctotf_17_res, nctotf_18_res, nctotf_19_res, nctotf_20_res,
       nctotf_21_res, nctotf_22_res, nctotf_23_res, nctotf_24_res, nctotf_25_res, nctotf_26_res,
       nctotf_27_res, nctotf_28_res, nctotf_29_res, nctotf_30_res, nctotf_31_res, nctotf_32_res,
       nctotf_33_res, nctotf_34_res, nctotf_35_res, nctotf_36_res, nctotf_37_res, nctotf_38_res,
       nctotf_39_res, nctotf_40_res, nctotf_41_res, nctotf_42_res, nctotf_43_res, nctotf_44_res,
       nctotf_45_res, nctotf_46_res, nctotf_47_res, nctotf_48_res, nctotf_49_res, nctotf_50_res,
       nctotf_51_res, nctotf_52_res, nctotf_53_res, nctotf_54_res, nctotf_55_res, nctotf_56_res,
       nctotf_57_res, nctotf_58_res, nctotf_59_res, nctotf_60_res, nctotf_61_res, nctotf_62_res,
       nctotf_63_res, nctotf_64_res, nctotf_65_res, nctotf_66_res, nctotf_67_res, nctotf_68_res,
       nctotf_69_res, nctotf_70_res, nctotf_71_res, nctotf_72_res, nctotf_73_res, nctotf_74_res,
       nctotf_75_res, nctotf_76_res, nctotf_77_res, nctotf_78_res, nctotf_79_res, nctotf_80_res,
       nctotf_81_res, nctotf_82_res, nctotf_83_res, nctotf_84_res, nctotf_85_res, nctotf_86_res,
       nctotf_87_res, nctotf_88_res, nctotf_89_res, nctotf_90_res, nctotf_91_res, nctotf_92_res,
       nctotf_93_res, nctotf_94_res, nctotf_95_res, nctotf_96_res, nctotf_97_res, nctotf_98_res,
       nctotf_99_res, nctotf_100_res, nctotf_101_res, nctotf_102_res, nctotf_103_res, nctotf_104_res,
       nctotf_105_res, nctotf_106_res, nctotf_107_res, nctotf_108_res, nctotf_109_res, nctotf_110_res,
       nctotf_119_res, nctotf_120_res, nctotf_121_res, nctotf_122_res, nctotf_123_res, nctotf_124_res,
       nctotf_125_res, nctotf_126_res, nctotf_127_res, nctotf_128_res, nctotf_129_res, nctotf_130_res,
       nctotf_131_res, nctotf_132_res, nctotf_133_res, nctotf_134_res, nctotf_135_res, not_1_out, or_1_out,
       or_2_out, or_3_out, or_5_out, or_6_out, or_8_out, or_9_out, or_10_out, or_11_out, or_12_out,
       or_13_out, or_14_out, or_15_out, or_16_out, or_17_out, or_18_out, or_19_out, or_20_out, or_21_out,
       or_22_out, or_24_out, or_25_out, or_27_out, or_28_out, or_29_out, por_1_out, Prepare_register_q,
       RESET_out, smallor_1_out_3, smallor_2_out_3, submod_1_carryout, submod_1_halfcarryout,
       submod_1_isazero, submod_1_negative, submod_1_signcarry, subtractor_1_bout, subtractor_2_bout,
       tftonc_1_res, tftonc_2_res, tftonc_3_res, tftonc_4_res, tftonc_9_res, tftonc_14_res, tftonc_22_res,
       tftonc_23_res, undriven_3, undriven_4, xor_1_out, xor_3_out, xor_4_out;
  wire [0:0] and_1_out;
  wire [1:0] or_7_out;
  wire [2:0] controlled_buffer_3_out;
  wire [4:0] controlled_buffer_3_out_2;
  wire [7:0] adder_3_out, adder_4_out, addmod_1_result, and_3_out, buscontrol_1_out_6, buscontrol_1_out_7,
       buscontrol_1_out_8, buscontrol_1_out_9, buscontrol_2_out_6, buscontrol_2_out_8, buscontrol_2_out_9,
       controlled_buffer_39_out, controlled_buffer_87_out, controlled_buffer_107_out,
       controlled_buffer_120_out, controlled_buffer_121_out, controlled_buffer_170_out, increment_1_b,
       increment_2_b, increment_3_b, increment_4_b, increment_5_b, increment_6_b, increment_7_b,
       increment_8_b, increment_9_b, increment_10_b, increment_11_b, increment_12_b, increment_13_b,
       increment_14_b, increment_15_b, increment_16_b, increment_17_b, increment_18_b, increment_19_b,
       increment_20_b, increment_21_b, increment_22_b, increment_23_b, increment_24_b, increment_25_b,
       increment_26_b, increment_27_b, increment_28_b, increment_29_b, increment_30_b, increment_31_b,
       increment_32_b, increment_33_b, increment_34_b, increment_35_b, JumpLeft_q, JumpRight_q,
       Main_Programm_p1, Main_Programm_p4, multiplexer_2_out, multiplexer_3_out, multiplexer_4_out,
       multiplexer_5_out, multiplexer_6_out, multiplexer_7_out, multiplexer_8_out, multiplexer_9_out,
       multiplexer_10_out, multiplexer_11_out, nctotf_111_res, or_23_out, ram_1_dout, register_1_q,
       register_2_q, register_3_q, register_4_q, register_5_q, register_6_q, register_7_q, register_8_q,
       register_9_q, register_10_q, register_11_q, register_12_q, register_13_q, register_14_q,
       register_15_q, register_16_q, register_17_q, register_18_q, register_19_q, register_20_q,
       register_21_q, register_22_q, register_23_q, register_24_q, register_25_q, register_26_q,
       register_27_q, register_35_q, submod_1_result, subtractor_1_out, undriven, undriven_2,
       Watchdog_Timer_Counter_q, X, xor_2_out, xor_5_out, Y;
  wire [7:7] and_2_out;
  wire [15:0] adder_1_out, adder_2_out, adder_5_out, controlled_buffer_75_out, counter_1_q, Main_Programm_p3,
       multiplexer_1_out, register_34_q, stack_1_out_6, stack_2_out_6;
  wire [15:8] buscontrol_2_out_7;
  wire [19:0] and_5_out, equals_131_res, not_2_out;
  wire [23:0] RGB;

  Button RESET (.out(RESET_out));
  or or_1 (or_1_out, RESET_out, por_1_out);
  buf buffer_1 (buffer_1_out, or_1_out);
  Button CONTINUE (.out(CONTINUE_out));
  Button HALT (.out(HALT_out));
  nand nand_1 (nand_1_out, buffer_1_out, ~or_2_out);  // NAND_Gate
  xor xor_1 (xor_1_out, nand_1_out, CONTINUE_out);
  or or_2 (or_2_out, HALT_out, nctotf_119_res);
  or or_3 (or_3_out, Reset_pin, equals_170_res);
  Clock Main_clock (.out(Main_clock_out));
  S_R_Flip_Flop Prepare_register (
    .S(xor_1_out), .R(1'b0), .clk(xor_1_out), .Q(Prepare_register_q), .reset(or_2_out));  // open: Qn, preset
  Counter #(.ongoal("stay")) Watchdog_Timer_Counter (
    .clr(or_3_out), .count(controlled_buffer_107_out[7]), .clk(controlled_buffer_1_out),
    .Q(Watchdog_Timer_Counter_q));  // open: load, up, D, carry
  Multiplexer #(.select(2), .width(16)) multiplexer_1 (
    .in0({JumpLeft_q, JumpRight_q}), .in1(controlled_buffer_75_out), .in2(adder_5_out), .in3(adder_5_out),
    .out(multiplexer_1_out), .sel(or_7_out));
  Counter #(.max('hffff), .ongoal("stay"), .width(16)) counter_1 (
    .load(nctotf_1_res), .D(multiplexer_1_out), .count(not_1_out), .Q(counter_1_q), .carry(counter_1_carry),
    .clk(controlled_buffer_1_out), .clr(smallor_1_out_3));  // open: up
  not not_1 (not_1_out, nctotf_1_res);
  smallOR smallor_1 (.in_1(Reset_pin), .out_3(smallor_1_out_3));  // open: in_2
  or or_4 (Reset_pin, RESET_out, por_1_out, nctotf_2_res);
  POR #(.PorHighDuration(1)) por_1 (.out(por_1_out));
  or or_5 (or_5_out, por_1_out, Main_clock_out);
  assign controlled_buffer_1_out = Prepare_register_q ? or_5_out : 1'bz;  // Controlled_Buffer controlled_buffer_1
  LED Counter_overflow (.in(counter_1_carry));
  NCtoTF nctotf_1 (.A(or_28_out), .res(nctotf_1_res));
  // Probe on Watchdog_Timer_Counter_q
  assign controlled_buffer_2_out = nctotf_3_res ? or_6_out : 1'bz;  // Controlled_Buffer controlled_buffer_2
  NCtoTF nctotf_2 (.A(controlled_buffer_2_out), .res(nctotf_2_res));
  NCtoTF nctotf_3 (.A(controlled_buffer_107_out[7]), .res(nctotf_3_res));
  or or_6 (or_6_out, comparator_1_gt, comparator_1_eq);
  Comparator #(.mode("unsigned")) comparator_1 (
    .a(Watchdog_Timer_Counter_q), .b(register_35_q), .gt(comparator_1_gt), .eq(comparator_1_eq));  // open: lt
  // ROM #(.addrWidth(18), .line("quad")) Main_Programm: pin names not known; wires that end beside it: Main_Programm_p1, Main_Programm_p3[15:8], Main_Programm_p3[7:0], Main_Programm_p4
  // Probe on buscontrol_1_out_8
  // Probe on buscontrol_1_out_9
  Register register_1 (
    .D(buscontrol_1_out_9), .en(nctotf_4_res), .clk(controlled_buffer_1_out), .Q(register_1_q),
    .clr(Reset_pin));
  Equals equals_1 (.A(buscontrol_1_out_8), .B({8{1'b0}}), .res(equals_1_res));
  NCtoTF nctotf_4 (.A(equals_1_res), .res(nctotf_4_res));
  Register register_2 (
    .D(buscontrol_1_out_9), .en(nctotf_5_res), .clk(controlled_buffer_1_out), .Q(register_2_q),
    .clr(Reset_pin));
  increment increment_1 (.A({8{1'b0}}), .B(increment_1_b));
  Equals equals_2 (.A(buscontrol_1_out_8), .B(increment_1_b), .res(equals_2_res));
  NCtoTF nctotf_5 (.A(equals_2_res), .res(nctotf_5_res));
  Register register_3 (
    .D(buscontrol_1_out_9), .en(nctotf_6_res), .clk(controlled_buffer_1_out), .Q(register_3_q),
    .clr(Reset_pin));
  increment increment_2 (.A(increment_1_b), .B(increment_2_b));
  Equals equals_3 (.A(buscontrol_1_out_8), .B(increment_2_b), .res(equals_3_res));
  NCtoTF nctotf_6 (.A(equals_3_res), .res(nctotf_6_res));
  Register register_4 (
    .D(buscontrol_1_out_9), .en(nctotf_7_res), .clk(controlled_buffer_1_out), .Q(register_4_q),
    .clr(Reset_pin));
  increment increment_3 (.A(increment_2_b), .B(increment_3_b));
  Equals equals_4 (.A(buscontrol_1_out_8), .B(increment_3_b), .res(equals_4_res));
  NCtoTF nctotf_7 (.A(equals_4_res), .res(nctotf_7_res));
  Register register_5 (
    .D(buscontrol_1_out_9), .en(nctotf_8_res), .clk(controlled_buffer_1_out), .Q(register_5_q),
    .clr(Reset_pin));
  increment increment_4 (.A(increment_3_b), .B(increment_4_b));
  Equals equals_5 (.A(buscontrol_1_out_8), .B(increment_4_b), .res(equals_5_res));
  NCtoTF nctotf_8 (.A(equals_5_res), .res(nctotf_8_res));
  Register register_6 (
    .D(buscontrol_1_out_9), .en(nctotf_9_res), .clk(controlled_buffer_1_out), .Q(register_6_q),
    .clr(Reset_pin));
  increment increment_5 (.A(increment_4_b), .B(increment_5_b));
  Equals equals_6 (.A(buscontrol_1_out_8), .B(increment_5_b), .res(equals_6_res));
  NCtoTF nctotf_9 (.A(equals_6_res), .res(nctotf_9_res));
  Register register_7 (
    .D(buscontrol_1_out_9), .en(nctotf_10_res), .clk(controlled_buffer_1_out), .Q(register_7_q),
    .clr(Reset_pin));
  increment increment_6 (.A(increment_5_b), .B(increment_6_b));
  Equals equals_7 (.A(buscontrol_1_out_8), .B(increment_6_b), .res(equals_7_res));
  NCtoTF nctotf_10 (.A(equals_7_res), .res(nctotf_10_res));
  Register register_8 (
    .D(buscontrol_1_out_9), .en(nctotf_11_res), .clk(controlled_buffer_1_out), .Q(register_8_q),
    .clr(Reset_pin));
  increment increment_7 (.A(increment_6_b), .B(increment_7_b));
  Equals equals_8 (.A(buscontrol_1_out_8), .B(increment_7_b), .res(equals_8_res));
  NCtoTF nctotf_11 (.A(equals_8_res), .res(nctotf_11_res));
  Register register_9 (
    .D(buscontrol_1_out_9), .en(nctotf_12_res), .clk(controlled_buffer_1_out), .Q(register_9_q),
    .clr(Reset_pin));
  increment increment_8 (.A(increment_7_b), .B(increment_8_b));
  Equals equals_9 (.A(buscontrol_1_out_8), .B(increment_8_b), .res(equals_9_res));
  NCtoTF nctotf_12 (.A(equals_9_res), .res(nctotf_12_res));
  Register register_10 (
    .D(buscontrol_1_out_9), .en(nctotf_13_res), .clk(controlled_buffer_1_out), .Q(register_10_q),
    .clr(Reset_pin));
  increment increment_9 (.A(increment_8_b), .B(increment_9_b));
  Equals equals_10 (.A(buscontrol_1_out_8), .B(increment_9_b), .res(equals_10_res));
  NCtoTF nctotf_13 (.A(equals_10_res), .res(nctotf_13_res));
  Register register_11 (
    .D(buscontrol_1_out_9), .en(nctotf_14_res), .clk(controlled_buffer_1_out), .Q(register_11_q),
    .clr(Reset_pin));
  increment increment_10 (.A(increment_9_b), .B(increment_10_b));
  Equals equals_11 (.A(buscontrol_1_out_8), .B(increment_10_b), .res(equals_11_res));
  NCtoTF nctotf_14 (.A(equals_11_res), .res(nctotf_14_res));
  Register register_12 (
    .D(buscontrol_1_out_9), .en(nctotf_15_res), .clk(controlled_buffer_1_out), .Q(register_12_q),
    .clr(Reset_pin));
  increment increment_11 (.A(increment_10_b), .B(increment_11_b));
  Equals equals_12 (.A(buscontrol_1_out_8), .B(increment_11_b), .res(equals_12_res));
  NCtoTF nctotf_15 (.A(equals_12_res), .res(nctotf_15_res));
  Register register_13 (
    .D(buscontrol_1_out_9), .en(nctotf_16_res), .clk(controlled_buffer_1_out), .Q(register_13_q),
    .clr(Reset_pin));
  increment increment_12 (.A(increment_11_b), .B(increment_12_b));
  Equals equals_13 (.A(buscontrol_1_out_8), .B(increment_12_b), .res(equals_13_res));
  NCtoTF nctotf_16 (.A(equals_13_res), .res(nctotf_16_res));
  Register register_14 (
    .D(buscontrol_1_out_9), .en(nctotf_17_res), .clk(controlled_buffer_1_out), .Q(register_14_q),
    .clr(Reset_pin));
  increment increment_13 (.A(increment_12_b), .B(increment_13_b));
  Equals equals_14 (.A(buscontrol_1_out_8), .B(increment_13_b), .res(equals_14_res));
  NCtoTF nctotf_17 (.A(equals_14_res), .res(nctotf_17_res));
  Register register_15 (
    .D(buscontrol_1_out_9), .en(nctotf_18_res), .clk(controlled_buffer_1_out), .Q(register_15_q),
    .clr(Reset_pin));
  increment increment_14 (.A(increment_13_b), .B(increment_14_b));
  Equals equals_15 (.A(buscontrol_1_out_8), .B(increment_14_b), .res(equals_15_res));
  NCtoTF nctotf_18 (.A(equals_15_res), .res(nctotf_18_res));
  Register register_16 (
    .D(buscontrol_1_out_9), .en(nctotf_19_res), .clk(controlled_buffer_1_out), .Q(register_16_q),
    .clr(Reset_pin));
  increment increment_15 (.A(increment_14_b), .B(increment_15_b));
  Equals equals_16 (.A(buscontrol_1_out_8), .B(increment_15_b), .res(equals_16_res));
  NCtoTF nctotf_19 (.A(equals_16_res), .res(nctotf_19_res));
  Register register_17 (
    .D(buscontrol_1_out_9), .en(nctotf_20_res), .clk(controlled_buffer_1_out), .Q(register_17_q),
    .clr(Reset_pin));
  increment increment_16 (.A(increment_15_b), .B(increment_16_b));
  Equals equals_17 (.A(buscontrol_1_out_8), .B(increment_16_b), .res(equals_17_res));
  NCtoTF nctotf_20 (.A(equals_17_res), .res(nctotf_20_res));
  Register register_18 (
    .D(buscontrol_1_out_9), .en(nctotf_21_res), .clk(controlled_buffer_1_out), .Q(register_18_q),
    .clr(Reset_pin));
  increment increment_17 (.A(increment_16_b), .B(increment_17_b));
  Equals equals_18 (.A(buscontrol_1_out_8), .B(increment_17_b), .res(equals_18_res));
  NCtoTF nctotf_21 (.A(equals_18_res), .res(nctotf_21_res));
  Register register_19 (
    .D(buscontrol_1_out_9), .en(nctotf_22_res), .clk(controlled_buffer_1_out), .Q(register_19_q),
    .clr(Reset_pin));
  increment increment_18 (.A(increment_17_b), .B(increment_18_b));
  Equals equals_19 (.A(buscontrol_1_out_8), .B(increment_18_b), .res(equals_19_res));
  NCtoTF nctotf_22 (.A(equals_19_res), .res(nctotf_22_res));
  Register register_20 (
    .D(buscontrol_1_out_9), .en(nctotf_23_res), .clk(controlled_buffer_1_out), .Q(register_20_q),
    .clr(Reset_pin));
  increment increment_19 (.A(increment_18_b), .B(increment_19_b));
  Equals equals_20 (.A(buscontrol_1_out_8), .B(increment_19_b), .res(equals_20_res));
  NCtoTF nctotf_23 (.A(equals_20_res), .res(nctotf_23_res));
  Register register_21 (
    .D(buscontrol_1_out_9), .en(nctotf_24_res), .clk(controlled_buffer_1_out), .Q(register_21_q),
    .clr(Reset_pin));
  increment increment_20 (.A(increment_19_b), .B(increment_20_b));
  Equals equals_21 (.A(buscontrol_1_out_8), .B(increment_20_b), .res(equals_21_res));
  NCtoTF nctotf_24 (.A(equals_21_res), .res(nctotf_24_res));
  Register register_22 (
    .D(buscontrol_1_out_9), .en(nctotf_25_res), .clk(controlled_buffer_1_out), .Q(register_22_q),
    .clr(Reset_pin));
  increment increment_21 (.A(increment_20_b), .B(increment_21_b));
  Equals equals_22 (.A(buscontrol_1_out_8), .B(increment_21_b), .res(equals_22_res));
  NCtoTF nctotf_25 (.A(equals_22_res), .res(nctotf_25_res));
  Register register_23 (
    .D(buscontrol_1_out_9), .en(nctotf_26_res), .clk(controlled_buffer_1_out), .Q(register_23_q),
    .clr(Reset_pin));
  increment increment_22 (.A(increment_21_b), .B(increment_22_b));
  Equals equals_23 (.A(buscontrol_1_out_8), .B(increment_22_b), .res(equals_23_res));
  NCtoTF nctotf_26 (.A(equals_23_res), .res(nctotf_26_res));
  Register register_24 (
    .D(buscontrol_1_out_9), .en(nctotf_27_res), .clk(controlled_buffer_1_out), .Q(register_24_q),
    .clr(Reset_pin));
  increment increment_23 (.A(increment_22_b), .B(increment_23_b));
  Equals equals_24 (.A(buscontrol_1_out_8), .B(increment_23_b), .res(equals_24_res));
  NCtoTF nctotf_27 (.A(equals_24_res), .res(nctotf_27_res));
  Register register_25 (
    .D(buscontrol_1_out_9), .en(nctotf_28_res), .clk(controlled_buffer_1_out), .Q(register_25_q),
    .clr(Reset_pin));
  increment increment_24 (.A(increment_23_b), .B(increment_24_b));
  Equals equals_25 (.A(buscontrol_1_out_8), .B(increment_24_b), .res(equals_25_res));
  NCtoTF nctotf_28 (.A(equals_25_res), .res(nctotf_28_res));
  Register register_26 (
    .D(buscontrol_1_out_9), .en(nctotf_29_res), .clk(controlled_buffer_1_out), .Q(register_26_q),
    .clr(Reset_pin));
  increment increment_25 (.A(increment_24_b), .B(increment_25_b));
  Equals equals_26 (.A(buscontrol_1_out_8), .B(increment_25_b), .res(equals_26_res));
  NCtoTF nctotf_29 (.A(equals_26_res), .res(nctotf_29_res));
  Register register_27 (
    .D(buscontrol_1_out_9), .en(nctotf_30_res), .clk(controlled_buffer_1_out), .Q(register_27_q),
    .clr(Reset_pin));
  increment increment_26 (.A(increment_25_b), .B(increment_26_b));
  Equals equals_27 (.A(buscontrol_1_out_8), .B(increment_26_b), .res(equals_27_res));
  NCtoTF nctotf_30 (.A(equals_27_res), .res(nctotf_30_res));
  Register register_28 (
    .D(buscontrol_1_out_9), .en(nctotf_31_res), .clk(controlled_buffer_1_out), .Q(X), .clr(Reset_pin));
  increment increment_27 (.A(increment_26_b), .B(increment_27_b));
  Equals equals_28 (.A(buscontrol_1_out_8), .B(increment_27_b), .res(equals_28_res));
  NCtoTF nctotf_31 (.A(equals_28_res), .res(nctotf_31_res));
  Register register_29 (
    .D(buscontrol_1_out_9), .en(nctotf_32_res), .clk(controlled_buffer_1_out), .Q(Y), .clr(Reset_pin));
  increment increment_28 (.A(increment_27_b), .B(increment_28_b));
  Equals equals_29 (.A(buscontrol_1_out_8), .B(increment_28_b), .res(equals_29_res));
  NCtoTF nctotf_32 (.A(equals_29_res), .res(nctotf_32_res));
  Register register_30 (
    .D(buscontrol_1_out_9), .en(nctotf_33_res), .clk(controlled_buffer_1_out), .Q(RGB[7:0]), .clr(Reset_pin));
  increment increment_29 (.A(increment_28_b), .B(increment_29_b));
  Equals equals_30 (.A(buscontrol_1_out_8), .B(increment_29_b), .res(equals_30_res));
  NCtoTF nctotf_33 (.A(equals_30_res), .res(nctotf_33_res));
  Register register_31 (
    .D(buscontrol_1_out_9), .en(nctotf_34_res), .clk(controlled_buffer_1_out), .Q(RGB[15:8]), .clr(Reset_pin));
  increment increment_30 (.A(increment_29_b), .B(increment_30_b));
  Equals equals_31 (.A(buscontrol_1_out_8), .B(increment_30_b), .res(equals_31_res));
  NCtoTF nctotf_34 (.A(equals_31_res), .res(nctotf_34_res));
  Register register_32 (
    .D(buscontrol_1_out_9), .en(nctotf_35_res), .clk(controlled_buffer_1_out), .Q(RGB[23:16]), .clr(Reset_pin));
  increment increment_31 (.A(increment_30_b), .B(increment_31_b));
  Equals equals_32 (.A(buscontrol_1_out_8), .B(increment_31_b), .res(equals_32_res));
  NCtoTF nctotf_35 (.A(equals_32_res), .res(nctotf_35_res));
  Register register_33 (
    .D(buscontrol_1_out_9), .en(nctotf_36_res), .clk(controlled_buffer_1_out), .Q(register_34_q[15:8]),
    .clr(Reset_pin));
  increment increment_32 (.A(increment_31_b), .B(increment_32_b));
  Equals equals_33 (.A(buscontrol_1_out_8), .B(increment_32_b), .res(equals_33_res));
  NCtoTF nctotf_36 (.A(equals_33_res), .res(nctotf_36_res));
  Register register_34 (
    .D(buscontrol_1_out_9), .en(nctotf_37_res), .clk(controlled_buffer_1_out), .Q(register_34_q[7:0]),
    .clr(Reset_pin));
  increment increment_33 (.A(increment_32_b), .B(increment_33_b));
  Equals equals_34 (.A(buscontrol_1_out_8), .B(increment_33_b), .res(equals_34_res));
  NCtoTF nctotf_37 (.A(equals_34_res), .res(nctotf_37_res));
  Register register_35 (
    .D(buscontrol_1_out_9), .en(nctotf_38_res), .clk(controlled_buffer_1_out), .Q(register_35_q));  // open: clr
  increment increment_34 (.A(increment_33_b), .B(increment_34_b));
  Equals equals_35 (.A(buscontrol_1_out_8), .B(increment_34_b), .res(equals_35_res));
  NCtoTF nctotf_38 (.A(equals_35_res), .res(nctotf_38_res));
  increment increment_35 (.A(increment_34_b), .B(increment_35_b));
  // DipSwitch K8: pin names not known
  Multiplexer #(.width(8)) multiplexer_2 (
    .in0(Main_Programm_p3[15:8]), .in1(controlled_buffer_39_out), .out(multiplexer_2_out),
    .sel(equals_129_res));
  Equals equals_36 (.A(buscontrol_1_out_7), .B({8{1'b0}}), .res(equals_36_res));
  NCtoTF nctotf_39 (.A(equals_36_res), .res(nctotf_39_res));
  assign {controlled_buffer_3_out_2, controlled_buffer_3_out} = nctotf_39_res ? register_1_q : 8'bz;  // Controlled_Buffer controlled_buffer_3
  Equals equals_37 (.A(buscontrol_1_out_6), .B({8{1'b0}}), .res(equals_37_res));
  Equals equals_38 (.A(buscontrol_1_out_7), .B(increment_1_b), .res(equals_38_res));
  NCtoTF nctotf_40 (.A(equals_38_res), .res(nctotf_40_res));
  assign {controlled_buffer_3_out_2, controlled_buffer_3_out} = nctotf_40_res ? register_2_q : 8'bz;  // Controlled_Buffer controlled_buffer_4
  Equals equals_39 (.A(buscontrol_1_out_6), .B(increment_1_b), .res(equals_39_res));
  Equals equals_40 (.A(buscontrol_1_out_7), .B(increment_2_b), .res(equals_40_res));
  NCtoTF nctotf_41 (.A(equals_40_res), .res(nctotf_41_res));
  assign {controlled_buffer_3_out_2, controlled_buffer_3_out} = nctotf_41_res ? register_3_q : 8'bz;  // Controlled_Buffer controlled_buffer_5
  Equals equals_41 (.A(buscontrol_1_out_6), .B(increment_2_b), .res(equals_41_res));
  Equals equals_42 (.A(buscontrol_1_out_7), .B(increment_3_b), .res(equals_42_res));
  NCtoTF nctotf_42 (.A(equals_42_res), .res(nctotf_42_res));
  assign {controlled_buffer_3_out_2, controlled_buffer_3_out} = nctotf_42_res ? register_4_q : 8'bz;  // Controlled_Buffer controlled_buffer_6
  Equals equals_43 (.A(buscontrol_1_out_6), .B(increment_3_b), .res(equals_43_res));
  Equals equals_44 (.A(buscontrol_1_out_7), .B(increment_4_b), .res(equals_44_res));
  NCtoTF nctotf_43 (.A(equals_44_res), .res(nctotf_43_res));
  assign {controlled_buffer_3_out_2, controlled_buffer_3_out} = nctotf_43_res ? register_5_q : 8'bz;  // Controlled_Buffer controlled_buffer_7
  Equals equals_45 (.A(buscontrol_1_out_6), .B(increment_4_b), .res(equals_45_res));
  Equals equals_46 (.A(buscontrol_1_out_7), .B(increment_5_b), .res(equals_46_res));
  NCtoTF nctotf_44 (.A(equals_46_res), .res(nctotf_44_res));
  assign {controlled_buffer_3_out_2, controlled_buffer_3_out} = nctotf_44_res ? register_6_q : 8'bz;  // Controlled_Buffer controlled_buffer_8
  Equals equals_47 (.A(buscontrol_1_out_6), .B(increment_5_b), .res(equals_47_res));
  Equals equals_48 (.A(buscontrol_1_out_7), .B(increment_6_b), .res(equals_48_res));
  NCtoTF nctotf_45 (.A(equals_48_res), .res(nctotf_45_res));
  assign {controlled_buffer_3_out_2, controlled_buffer_3_out} = nctotf_45_res ? register_7_q : 8'bz;  // Controlled_Buffer controlled_buffer_9
  Equals equals_49 (.A(buscontrol_1_out_6), .B(increment_6_b), .res(equals_49_res));
  Equals equals_50 (.A(buscontrol_1_out_7), .B(increment_7_b), .res(equals_50_res));
  NCtoTF nctotf_46 (.A(equals_50_res), .res(nctotf_46_res));
  assign {controlled_buffer_3_out_2, controlled_buffer_3_out} = nctotf_46_res ? register_8_q : 8'bz;  // Controlled_Buffer controlled_buffer_10
  Equals equals_51 (.A(buscontrol_1_out_6), .B(increment_7_b), .res(equals_51_res));
  Equals equals_52 (.A(buscontrol_1_out_7), .B(increment_8_b), .res(equals_52_res));
  NCtoTF nctotf_47 (.A(equals_52_res), .res(nctotf_47_res));
  assign {controlled_buffer_3_out_2, controlled_buffer_3_out} = nctotf_47_res ? register_9_q : 8'bz;  // Controlled_Buffer controlled_buffer_11
  Equals equals_53 (.A(buscontrol_1_out_6), .B(increment_8_b), .res(equals_53_res));
  Equals equals_54 (.A(buscontrol_1_out_7), .B(increment_9_b), .res(equals_54_res));
  NCtoTF nctotf_48 (.A(equals_54_res), .res(nctotf_48_res));
  assign {controlled_buffer_3_out_2, controlled_buffer_3_out} = nctotf_48_res ? register_10_q : 8'bz;  // Controlled_Buffer controlled_buffer_12
  Equals equals_55 (.A(buscontrol_1_out_6), .B(increment_9_b), .res(equals_55_res));
  Equals equals_56 (.A(buscontrol_1_out_7), .B(increment_10_b), .res(equals_56_res));
  NCtoTF nctotf_49 (.A(equals_56_res), .res(nctotf_49_res));
  assign {controlled_buffer_3_out_2, controlled_buffer_3_out} = nctotf_49_res ? register_11_q : 8'bz;  // Controlled_Buffer controlled_buffer_13
  Equals equals_57 (.A(buscontrol_1_out_6), .B(increment_10_b), .res(equals_57_res));
  Equals equals_58 (.A(buscontrol_1_out_7), .B(increment_11_b), .res(equals_58_res));
  NCtoTF nctotf_50 (.A(equals_58_res), .res(nctotf_50_res));
  assign {controlled_buffer_3_out_2, controlled_buffer_3_out} = nctotf_50_res ? register_12_q : 8'bz;  // Controlled_Buffer controlled_buffer_14
  Equals equals_59 (.A(buscontrol_1_out_6), .B(increment_11_b), .res(equals_59_res));
  Equals equals_60 (.A(buscontrol_1_out_7), .B(increment_12_b), .res(equals_60_res));
  NCtoTF nctotf_51 (.A(equals_60_res), .res(nctotf_51_res));
  assign {controlled_buffer_3_out_2, controlled_buffer_3_out} = nctotf_51_res ? register_13_q : 8'bz;  // Controlled_Buffer controlled_buffer_15
  Equals equals_61 (.A(buscontrol_1_out_6), .B(increment_12_b), .res(equals_61_res));
  Equals equals_62 (.A(buscontrol_1_out_7), .B(increment_13_b), .res(equals_62_res));
  NCtoTF nctotf_52 (.A(equals_62_res), .res(nctotf_52_res));
  assign {controlled_buffer_3_out_2, controlled_buffer_3_out} = nctotf_52_res ? register_14_q : 8'bz;  // Controlled_Buffer controlled_buffer_16
  Equals equals_63 (.A(buscontrol_1_out_6), .B(increment_13_b), .res(equals_63_res));
  Equals equals_64 (.A(buscontrol_1_out_7), .B(increment_14_b), .res(equals_64_res));
  NCtoTF nctotf_53 (.A(equals_64_res), .res(nctotf_53_res));
  assign {controlled_buffer_3_out_2, controlled_buffer_3_out} = nctotf_53_res ? register_15_q : 8'bz;  // Controlled_Buffer controlled_buffer_17
  Equals equals_65 (.A(buscontrol_1_out_6), .B(increment_14_b), .res(equals_65_res));
  Equals equals_66 (.A(buscontrol_1_out_7), .B(increment_15_b), .res(equals_66_res));
  NCtoTF nctotf_54 (.A(equals_66_res), .res(nctotf_54_res));
  assign {controlled_buffer_3_out_2, controlled_buffer_3_out} = nctotf_54_res ? register_16_q : 8'bz;  // Controlled_Buffer controlled_buffer_18
  Equals equals_67 (.A(buscontrol_1_out_6), .B(increment_15_b), .res(equals_67_res));
  Equals equals_68 (.A(buscontrol_1_out_7), .B(increment_16_b), .res(equals_68_res));
  NCtoTF nctotf_55 (.A(equals_68_res), .res(nctotf_55_res));
  assign {controlled_buffer_3_out_2, controlled_buffer_3_out} = nctotf_55_res ? register_17_q : 8'bz;  // Controlled_Buffer controlled_buffer_19
  Equals equals_69 (.A(buscontrol_1_out_6), .B(increment_16_b), .res(equals_69_res));
  Equals equals_70 (.A(buscontrol_1_out_7), .B(increment_17_b), .res(equals_70_res));
  NCtoTF nctotf_56 (.A(equals_70_res), .res(nctotf_56_res));
  assign {controlled_buffer_3_out_2, controlled_buffer_3_out} = nctotf_56_res ? register_18_q : 8'bz;  // Controlled_Buffer controlled_buffer_20
  Equals equals_71 (.A(buscontrol_1_out_6), .B(increment_17_b), .res(equals_71_res));
  Equals equals_72 (.A(buscontrol_1_out_7), .B(increment_18_b), .res(equals_72_res));
  NCtoTF nctotf_57 (.A(equals_72_res), .res(nctotf_57_res));
  assign {controlled_buffer_3_out_2, controlled_buffer_3_out} = nctotf_57_res ? register_19_q : 8'bz;  // Controlled_Buffer controlled_buffer_21
  Equals equals_73 (.A(buscontrol_1_out_6), .B(increment_18_b), .res(equals_73_res));
  Equals equals_74 (.A(buscontrol_1_out_7), .B(increment_19_b), .res(equals_74_res));
  NCtoTF nctotf_58 (.A(equals_74_res), .res(nctotf_58_res));
  assign {controlled_buffer_3_out_2, controlled_buffer_3_out} = nctotf_58_res ? register_20_q : 8'bz;  // Controlled_Buffer controlled_buffer_22
  Equals equals_75 (.A(buscontrol_1_out_6), .B(increment_19_b), .res(equals_75_res));
  Equals equals_76 (.A(buscontrol_1_out_7), .B(increment_20_b), .res(equals_76_res));
  NCtoTF nctotf_59 (.A(equals_76_res), .res(nctotf_59_res));
  assign {controlled_buffer_3_out_2, controlled_buffer_3_out} = nctotf_59_res ? register_21_q : 8'bz;  // Controlled_Buffer controlled_buffer_23
  Equals equals_77 (.A(buscontrol_1_out_6), .B(increment_20_b), .res(equals_77_res));
  Equals equals_78 (.A(buscontrol_1_out_7), .B(increment_21_b), .res(equals_78_res));
  NCtoTF nctotf_60 (.A(equals_78_res), .res(nctotf_60_res));
  assign {controlled_buffer_3_out_2, controlled_buffer_3_out} = nctotf_60_res ? register_22_q : 8'bz;  // Controlled_Buffer controlled_buffer_24
  Equals equals_79 (.A(buscontrol_1_out_6), .B(increment_21_b), .res(equals_79_res));
  Equals equals_80 (.A(buscontrol_1_out_7), .B(increment_22_b), .res(equals_80_res));
  NCtoTF nctotf_61 (.A(equals_80_res), .res(nctotf_61_res));
  assign {controlled_buffer_3_out_2, controlled_buffer_3_out} = nctotf_61_res ? register_23_q : 8'bz;  // Controlled_Buffer controlled_buffer_25
  Equals equals_81 (.A(buscontrol_1_out_6), .B(increment_22_b), .res(equals_81_res));
  Equals equals_82 (.A(buscontrol_1_out_7), .B(increment_23_b), .res(equals_82_res));
  NCtoTF nctotf_62 (.A(equals_82_res), .res(nctotf_62_res));
  assign {controlled_buffer_3_out_2, controlled_buffer_3_out} = nctotf_62_res ? register_24_q : 8'bz;  // Controlled_Buffer controlled_buffer_26
  Equals equals_83 (.A(buscontrol_1_out_6), .B(increment_23_b), .res(equals_83_res));
  Equals equals_84 (.A(buscontrol_1_out_7), .B(increment_24_b), .res(equals_84_res));
  NCtoTF nctotf_63 (.A(equals_84_res), .res(nctotf_63_res));
  assign {controlled_buffer_3_out_2, controlled_buffer_3_out} = nctotf_63_res ? register_25_q : 8'bz;  // Controlled_Buffer controlled_buffer_27
  Equals equals_85 (.A(buscontrol_1_out_6), .B(increment_24_b), .res(equals_85_res));
  Equals equals_86 (.A(buscontrol_1_out_7), .B(increment_25_b), .res(equals_86_res));
  NCtoTF nctotf_64 (.A(equals_86_res), .res(nctotf_64_res));
  assign {controlled_buffer_3_out_2, controlled_buffer_3_out} = nctotf_64_res ? register_26_q : 8'bz;  // Controlled_Buffer controlled_buffer_28
  Equals equals_87 (.A(buscontrol_1_out_6), .B(increment_25_b), .res(equals_87_res));
  Equals equals_88 (.A(buscontrol_1_out_7), .B(increment_26_b), .res(equals_88_res));
  NCtoTF nctotf_65 (.A(equals_88_res), .res(nctotf_65_res));
  assign {controlled_buffer_3_out_2, controlled_buffer_3_out} = nctotf_65_res ? register_27_q : 8'bz;  // Controlled_Buffer controlled_buffer_29
  Equals equals_89 (.A(buscontrol_1_out_6), .B(increment_26_b), .res(equals_89_res));
  Equals equals_90 (.A(buscontrol_1_out_7), .B(increment_27_b), .res(equals_90_res));
  NCtoTF nctotf_66 (.A(equals_90_res), .res(nctotf_66_res));
  assign {controlled_buffer_3_out_2, controlled_buffer_3_out} = nctotf_66_res ? X : 8'bz;  // Controlled_Buffer controlled_buffer_30
  Equals equals_91 (.A(buscontrol_1_out_6), .B(increment_27_b), .res(equals_91_res));
  Equals equals_92 (.A(buscontrol_1_out_7), .B(increment_28_b), .res(equals_92_res));
  NCtoTF nctotf_67 (.A(equals_92_res), .res(nctotf_67_res));
  assign {controlled_buffer_3_out_2, controlled_buffer_3_out} = nctotf_67_res ? Y : 8'bz;  // Controlled_Buffer controlled_buffer_31
  Equals equals_93 (.A(buscontrol_1_out_6), .B(increment_28_b), .res(equals_93_res));
  Equals equals_94 (.A(buscontrol_1_out_7), .B(increment_29_b), .res(equals_94_res));
  NCtoTF nctotf_68 (.A(equals_94_res), .res(nctotf_68_res));
  assign {controlled_buffer_3_out_2, controlled_buffer_3_out} = nctotf_68_res ? RGB[7:0] : 8'bz;  // Controlled_Buffer controlled_buffer_32
  Equals equals_95 (.A(buscontrol_1_out_6), .B(increment_29_b), .res(equals_95_res));
  Equals equals_96 (.A(buscontrol_1_out_7), .B(increment_30_b), .res(equals_96_res));
  NCtoTF nctotf_69 (.A(equals_96_res), .res(nctotf_69_res));
  assign {controlled_buffer_3_out_2, controlled_buffer_3_out} = nctotf_69_res ? RGB[15:8] : 8'bz;  // Controlled_Buffer controlled_buffer_33
  Equals equals_97 (.A(buscontrol_1_out_6), .B(increment_30_b), .res(equals_97_res));
  Equals equals_98 (.A(buscontrol_1_out_7), .B(increment_31_b), .res(equals_98_res));
  NCtoTF nctotf_70 (.A(equals_98_res), .res(nctotf_70_res));
  assign {controlled_buffer_3_out_2, controlled_buffer_3_out} = nctotf_70_res ? RGB[23:16] : 8'bz;  // Controlled_Buffer controlled_buffer_34
  Equals equals_99 (.A(buscontrol_1_out_6), .B(increment_31_b), .res(equals_99_res));
  Equals equals_100 (.A(buscontrol_1_out_7), .B(increment_32_b), .res(equals_100_res));
  NCtoTF nctotf_71 (.A(equals_100_res), .res(nctotf_71_res));
  assign {controlled_buffer_3_out_2, controlled_buffer_3_out} = nctotf_71_res ? register_34_q[15:8] : 8'bz;  // Controlled_Buffer controlled_buffer_35
  Equals equals_101 (.A(buscontrol_1_out_6), .B(increment_32_b), .res(equals_101_res));
  Equals equals_102 (.A(buscontrol_1_out_7), .B(increment_33_b), .res(equals_102_res));
  NCtoTF nctotf_72 (.A(equals_102_res), .res(nctotf_72_res));
  assign {controlled_buffer_3_out_2, controlled_buffer_3_out} = nctotf_72_res ? register_34_q[7:0] : 8'bz;  // Controlled_Buffer controlled_buffer_36
  Equals equals_103 (.A(buscontrol_1_out_6), .B(increment_33_b), .res(equals_103_res));
  Equals equals_104 (.A(buscontrol_1_out_7), .B(increment_34_b), .res(equals_104_res));
  NCtoTF nctotf_73 (.A(equals_104_res), .res(nctotf_73_res));
  assign {controlled_buffer_3_out_2, controlled_buffer_3_out} = nctotf_73_res ? register_35_q : 8'bz;  // Controlled_Buffer controlled_buffer_37
  Equals equals_105 (.A(buscontrol_1_out_6), .B(increment_34_b), .res(equals_105_res));
  Equals equals_106 (.A(buscontrol_1_out_7), .B(increment_35_b), .res(equals_106_res));
  NCtoTF nctotf_74 (.A(equals_106_res), .res(nctotf_74_res));
  assign {controlled_buffer_3_out_2, controlled_buffer_3_out} = nctotf_74_res ? undriven : 8'bz;  // Controlled_Buffer controlled_buffer_38
  Equals equals_107 (.A(increment_35_b), .res(equals_107_res));  // open: B
  Register JumpLeft (
    .D(multiplexer_2_out), .en(or_21_out), .clk(controlled_buffer_1_out), .Q(JumpLeft_q), .clr(Reset_pin));
  NCtoTF nctotf_75 (.A(equals_37_res), .res(nctotf_75_res));
  assign controlled_buffer_39_out = nctotf_75_res ? register_1_q : 8'bz;  // Controlled_Buffer controlled_buffer_39
  NCtoTF nctotf_76 (.A(equals_39_res), .res(nctotf_76_res));
  assign controlled_buffer_39_out = nctotf_76_res ? register_2_q : 8'bz;  // Controlled_Buffer controlled_buffer_40
  NCtoTF nctotf_77 (.A(equals_41_res), .res(nctotf_77_res));
  assign controlled_buffer_39_out = nctotf_77_res ? register_3_q : 8'bz;  // Controlled_Buffer controlled_buffer_41
  NCtoTF nctotf_78 (.A(equals_43_res), .res(nctotf_78_res));
  assign controlled_buffer_39_out = nctotf_78_res ? register_4_q : 8'bz;  // Controlled_Buffer controlled_buffer_42
  NCtoTF nctotf_79 (.A(equals_45_res), .res(nctotf_79_res));
  assign controlled_buffer_39_out = nctotf_79_res ? register_5_q : 8'bz;  // Controlled_Buffer controlled_buffer_43
  NCtoTF nctotf_80 (.A(equals_47_res), .res(nctotf_80_res));
  assign controlled_buffer_39_out = nctotf_80_res ? register_6_q : 8'bz;  // Controlled_Buffer controlled_buffer_44
  NCtoTF nctotf_81 (.A(equals_49_res), .res(nctotf_81_res));
  assign controlled_buffer_39_out = nctotf_81_res ? register_7_q : 8'bz;  // Controlled_Buffer controlled_buffer_45
  NCtoTF nctotf_82 (.A(equals_51_res), .res(nctotf_82_res));
  assign controlled_buffer_39_out = nctotf_82_res ? register_8_q : 8'bz;  // Controlled_Buffer controlled_buffer_46
  NCtoTF nctotf_83 (.A(equals_53_res), .res(nctotf_83_res));
  assign controlled_buffer_39_out = nctotf_83_res ? register_9_q : 8'bz;  // Controlled_Buffer controlled_buffer_47
  NCtoTF nctotf_84 (.A(equals_55_res), .res(nctotf_84_res));
  assign controlled_buffer_39_out = nctotf_84_res ? register_10_q : 8'bz;  // Controlled_Buffer controlled_buffer_48
  NCtoTF nctotf_85 (.A(equals_57_res), .res(nctotf_85_res));
  assign controlled_buffer_39_out = nctotf_85_res ? register_11_q : 8'bz;  // Controlled_Buffer controlled_buffer_49
  NCtoTF nctotf_86 (.A(equals_59_res), .res(nctotf_86_res));
  assign controlled_buffer_39_out = nctotf_86_res ? register_12_q : 8'bz;  // Controlled_Buffer controlled_buffer_50
  NCtoTF nctotf_87 (.A(equals_61_res), .res(nctotf_87_res));
  assign controlled_buffer_39_out = nctotf_87_res ? register_13_q : 8'bz;  // Controlled_Buffer controlled_buffer_51
  NCtoTF nctotf_88 (.A(equals_63_res), .res(nctotf_88_res));
  assign controlled_buffer_39_out = nctotf_88_res ? register_14_q : 8'bz;  // Controlled_Buffer controlled_buffer_52
  NCtoTF nctotf_89 (.A(equals_65_res), .res(nctotf_89_res));
  assign controlled_buffer_39_out = nctotf_89_res ? register_15_q : 8'bz;  // Controlled_Buffer controlled_buffer_53
  NCtoTF nctotf_90 (.A(equals_67_res), .res(nctotf_90_res));
  assign controlled_buffer_39_out = nctotf_90_res ? register_16_q : 8'bz;  // Controlled_Buffer controlled_buffer_54
  NCtoTF nctotf_91 (.A(equals_69_res), .res(nctotf_91_res));
  assign controlled_buffer_39_out = nctotf_91_res ? register_17_q : 8'bz;  // Controlled_Buffer controlled_buffer_55
  NCtoTF nctotf_92 (.A(equals_71_res), .res(nctotf_92_res));
  assign controlled_buffer_39_out = nctotf_92_res ? register_18_q : 8'bz;  // Controlled_Buffer controlled_buffer_56
  NCtoTF nctotf_93 (.A(equals_73_res), .res(nctotf_93_res));
  assign controlled_buffer_39_out = nctotf_93_res ? register_19_q : 8'bz;  // Controlled_Buffer controlled_buffer_57
  NCtoTF nctotf_94 (.A(equals_75_res), .res(nctotf_94_res));
  assign controlled_buffer_39_out = nctotf_94_res ? register_20_q : 8'bz;  // Controlled_Buffer controlled_buffer_58
  NCtoTF nctotf_95 (.A(equals_77_res), .res(nctotf_95_res));
  assign controlled_buffer_39_out = nctotf_95_res ? register_21_q : 8'bz;  // Controlled_Buffer controlled_buffer_59
  NCtoTF nctotf_96 (.A(equals_79_res), .res(nctotf_96_res));
  assign controlled_buffer_39_out = nctotf_96_res ? register_22_q : 8'bz;  // Controlled_Buffer controlled_buffer_60
  NCtoTF nctotf_97 (.A(equals_81_res), .res(nctotf_97_res));
  assign controlled_buffer_39_out = nctotf_97_res ? register_23_q : 8'bz;  // Controlled_Buffer controlled_buffer_61
  NCtoTF nctotf_98 (.A(equals_83_res), .res(nctotf_98_res));
  assign controlled_buffer_39_out = nctotf_98_res ? register_24_q : 8'bz;  // Controlled_Buffer controlled_buffer_62
  NCtoTF nctotf_99 (.A(equals_85_res), .res(nctotf_99_res));
  assign controlled_buffer_39_out = nctotf_99_res ? register_25_q : 8'bz;  // Controlled_Buffer controlled_buffer_63
  NCtoTF nctotf_100 (.A(equals_87_res), .res(nctotf_100_res));
  assign controlled_buffer_39_out = nctotf_100_res ? register_26_q : 8'bz;  // Controlled_Buffer controlled_buffer_64
  NCtoTF nctotf_101 (.A(equals_89_res), .res(nctotf_101_res));
  assign controlled_buffer_39_out = nctotf_101_res ? register_27_q : 8'bz;  // Controlled_Buffer controlled_buffer_65
  NCtoTF nctotf_102 (.A(equals_91_res), .res(nctotf_102_res));
  assign controlled_buffer_39_out = nctotf_102_res ? X : 8'bz;  // Controlled_Buffer controlled_buffer_66
  NCtoTF nctotf_103 (.A(equals_93_res), .res(nctotf_103_res));
  assign controlled_buffer_39_out = nctotf_103_res ? Y : 8'bz;  // Controlled_Buffer controlled_buffer_67
  NCtoTF nctotf_104 (.A(equals_95_res), .res(nctotf_104_res));
  assign controlled_buffer_39_out = nctotf_104_res ? RGB[7:0] : 8'bz;  // Controlled_Buffer controlled_buffer_68
  NCtoTF nctotf_105 (.A(equals_97_res), .res(nctotf_105_res));
  assign controlled_buffer_39_out = nctotf_105_res ? RGB[15:8] : 8'bz;  // Controlled_Buffer controlled_buffer_69
  NCtoTF nctotf_106 (.A(equals_99_res), .res(nctotf_106_res));
  assign controlled_buffer_39_out = nctotf_106_res ? RGB[23:16] : 8'bz;  // Controlled_Buffer controlled_buffer_70
  NCtoTF nctotf_107 (.A(equals_101_res), .res(nctotf_107_res));
  assign controlled_buffer_39_out = nctotf_107_res ? register_34_q[15:8] : 8'bz;  // Controlled_Buffer controlled_buffer_71
  NCtoTF nctotf_108 (.A(equals_103_res), .res(nctotf_108_res));
  assign controlled_buffer_39_out = nctotf_108_res ? register_34_q[7:0] : 8'bz;  // Controlled_Buffer controlled_buffer_72
  NCtoTF nctotf_109 (.A(equals_105_res), .res(nctotf_109_res));
  assign controlled_buffer_39_out = nctotf_109_res ? register_35_q : 8'bz;  // Controlled_Buffer controlled_buffer_73
  NCtoTF nctotf_110 (.A(equals_107_res), .res(nctotf_110_res));
  assign controlled_buffer_39_out = nctotf_110_res ? undriven : 8'bz;  // Controlled_Buffer controlled_buffer_74
  Register JumpRight (
    .D(multiplexer_3_out), .en(or_21_out), .clk(controlled_buffer_1_out), .Q(JumpRight_q), .clr(Reset_pin));
  Multiplexer #(.width(8)) multiplexer_3 (
    .in0(Main_Programm_p3[7:0]), .in1({controlled_buffer_3_out_2, controlled_buffer_3_out}),
    .out(multiplexer_3_out), .sel(equals_129_res));
  busControl buscontrol_1 (
    .in_1(buscontrol_2_out_8), .in_2(buscontrol_2_out_7), .in_3(controlled_buffer_121_out),
    .in_4(controlled_buffer_120_out), .in_5(Prepare_register_q), .out_6(buscontrol_1_out_6),
    .out_7(buscontrol_1_out_7), .out_8(buscontrol_1_out_8), .out_9(buscontrol_1_out_9));
  // Probe on {JumpLeft_q, JumpRight_q}
  // Probe on Main_Programm_p1
  // Probe on Main_Programm_p3
  // Probe on Main_Programm_p3[15:8]
  // Probe on Main_Programm_p3[7:0]
  or or_7 (or_7_out[0], equals_153_res, equals_151_res);
  // Probe on Main_Programm_p4
  busControl buscontrol_2 (
    .in_1(Main_Programm_p1), .in_2(Main_Programm_p3[15:8]), .in_3(Main_Programm_p3[7:0]),
    .in_4(Main_Programm_p4), .in_5(Prepare_register_q), .out_6(buscontrol_2_out_6),
    .out_7(buscontrol_2_out_7), .out_8(buscontrol_2_out_8), .out_9(buscontrol_2_out_9));
  Equals equals_108 (.A(buscontrol_2_out_6), .B({8{1'b0}}), .res(equals_108_res));
  Equals equals_109 (.A(buscontrol_2_out_6), .B(8'h1), .res(equals_109_res));
  Equals equals_110 (.A(buscontrol_2_out_6), .B(8'h2), .res(equals_110_res));
  Equals equals_111 (.A(buscontrol_2_out_6), .B(8'h3), .res(equals_111_res));
  Equals equals_112 (.A(buscontrol_2_out_6), .B(8'h4), .res(equals_112_res));
  Equals equals_113 (.A(buscontrol_2_out_6), .B(8'h5), .res(equals_113_res));
  Equals equals_114 (.A(buscontrol_2_out_6), .B(8'h6), .res(equals_114_res));
  Equals equals_115 (.A(buscontrol_2_out_6), .B(8'h7), .res(equals_115_res));
  Equals equals_116 (.A(buscontrol_2_out_6), .B(8'h8), .res(equals_116_res));
  Equals equals_117 (.A(buscontrol_2_out_6), .B(8'h9), .res(equals_117_res));
  Equals equals_118 (.A(buscontrol_2_out_6), .B(8'ha), .res(equals_118_res));
  Equals equals_119 (.A(buscontrol_2_out_6), .B(8'hb), .res(equals_119_res));
  Equals equals_120 (.A(buscontrol_2_out_6), .B(8'hc), .res(equals_120_res));
  Equals equals_121 (.A(buscontrol_2_out_6), .B(8'hd), .res(equals_121_res));
  Equals equals_122 (.A(buscontrol_2_out_6), .B(8'he), .res(equals_122_res));
  Equals equals_123 (.A(buscontrol_2_out_6), .B(8'hf), .res(equals_123_res));
  Equals equals_124 (.A(buscontrol_2_out_6), .B(8'h10), .res(equals_124_res));
  Equals equals_125 (.A(buscontrol_2_out_6), .B(8'h11), .res(equals_125_res));
  Equals equals_126 (.A(buscontrol_2_out_6), .B(8'h12), .res(equals_126_res));
  NCtoTF nctotf_111 (.A(controlled_buffer_3_out[0]), .res(nctotf_111_res[0]));
  NCtoTF nctotf_112 (.A(controlled_buffer_3_out[1]), .res(nctotf_111_res[1]));
  NCtoTF nctotf_113 (.A(controlled_buffer_3_out[2]), .res(nctotf_111_res[2]));
  NCtoTF nctotf_114 (.A(controlled_buffer_3_out_2[0]), .res(nctotf_111_res[3]));
  NCtoTF nctotf_115 (.A(controlled_buffer_3_out_2[1]), .res(nctotf_111_res[4]));
  NCtoTF nctotf_116 (.A(controlled_buffer_3_out_2[2]), .res(nctotf_111_res[5]));
  NCtoTF nctotf_117 (.A(controlled_buffer_3_out_2[3]), .res(nctotf_111_res[6]));
  NCtoTF nctotf_118 (.A(controlled_buffer_3_out_2[4]), .res(nctotf_111_res[7]));
  Equals equals_127 (.A(buscontrol_2_out_6), .B(8'h13), .res(equals_127_res));
  Equals equals_128 (.A(buscontrol_2_out_6), .B(8'h14), .res(equals_128_res));
  Equals equals_129 (.A(buscontrol_2_out_6), .B(8'h15), .res(equals_129_res));
  Equals equals_130 (.A(buscontrol_2_out_6), .B(8'h16), .res(equals_130_res));
  Equals equals_131 (.A(buscontrol_2_out_6), .B(8'h17), .res(equals_131_res[0]));
  Equals equals_132 (.A(buscontrol_2_out_6), .B(8'h18), .res(equals_131_res[1]));
  Equals equals_133 (.A(buscontrol_2_out_6), .B(8'h19), .res(equals_131_res[2]));
  Equals equals_134 (.A(buscontrol_2_out_6), .B(8'h1a), .res(equals_131_res[3]));
  Equals equals_135 (.A(buscontrol_2_out_6), .B(8'h1b), .res(equals_131_res[4]));
  Equals equals_136 (.A(buscontrol_2_out_6), .B(8'h1c), .res(equals_131_res[5]));
  Equals equals_137 (.A(buscontrol_2_out_6), .B(8'h1d), .res(equals_131_res[6]));
  Equals equals_138 (.A(buscontrol_2_out_6), .B(8'h1e), .res(equals_131_res[7]));
  Equals equals_139 (.A(buscontrol_2_out_6), .B(8'h1f), .res(equals_131_res[8]));
  Equals equals_140 (.A(buscontrol_2_out_6), .B(8'h20), .res(equals_131_res[9]));
  Equals equals_141 (.A(buscontrol_2_out_6), .B(8'h21), .res(equals_131_res[10]));
  Equals equals_142 (.A(buscontrol_2_out_6), .B(8'h22), .res(equals_131_res[11]));
  Equals equals_143 (.A(buscontrol_2_out_6), .B(8'h23), .res(equals_131_res[12]));
  Equals equals_144 (.A(buscontrol_2_out_6), .B(8'h24), .res(equals_131_res[13]));
  Equals equals_145 (.A(buscontrol_2_out_6), .B(8'h25), .res(equals_131_res[14]));
  Equals equals_146 (.A(buscontrol_2_out_6), .B(8'h26), .res(equals_131_res[15]));
  Equals equals_147 (.A(buscontrol_2_out_6), .B(8'h27), .res(equals_131_res[16]));
  Equals equals_148 (.A(buscontrol_2_out_6), .B(8'h28), .res(equals_131_res[17]));
  Equals equals_149 (.A(buscontrol_2_out_6), .B(8'h29), .res(equals_131_res[18]));
  Equals equals_150 (.A(buscontrol_2_out_6), .B(8'h2a), .res(equals_131_res[19]));
  BitSelector bitselector_1 (.in(controlled_buffer_107_out), .out(not_2_out[1]), .sel(buscontrol_2_out_7[10:8]));
  Equals equals_151 (.A(buscontrol_2_out_6), .B(8'h2b), .res(equals_151_res));
  Equals equals_152 (.A(buscontrol_2_out_6), .B(8'h2c), .res(equals_152_res));
  assign controlled_buffer_75_out = equals_151_res ? adder_1_out : 16'bz;  // Controlled_Buffer controlled_buffer_75
  Equals equals_153 (.A(buscontrol_2_out_6), .B(8'h2d), .res(equals_153_res));
  Equals equals_154 (.A(buscontrol_2_out_6), .B(8'h2e), .res(equals_154_res));
  assign controlled_buffer_75_out = equals_153_res ? adder_2_out : 16'bz;  // Controlled_Buffer controlled_buffer_76
  Equals equals_155 (.A(buscontrol_2_out_6), .B(8'h2f), .res(or_7_out[1]));
  Equals equals_156 (.A(buscontrol_2_out_6), .B(8'h30), .res(equals_156_res));
  Equals equals_157 (.A(buscontrol_2_out_6), .B(8'h31), .res(equals_157_res));
  Equals equals_158 (.A(buscontrol_2_out_6), .B(8'h32), .res(equals_158_res));
  Equals equals_159 (.A(buscontrol_2_out_6), .B(8'h33), .res(equals_159_res));
  Equals equals_160 (.A(buscontrol_2_out_6), .B(8'h34), .res(equals_160_res));
  Equals equals_161 (.A(buscontrol_2_out_6), .B(8'h35), .res(equals_161_res));
  Equals equals_162 (.A(buscontrol_2_out_6), .B(8'h36), .res(equals_162_res));
  Equals equals_163 (.A(buscontrol_2_out_6), .B(8'h37), .res(equals_163_res));
  Equals equals_164 (.A(buscontrol_2_out_6), .B(8'h38), .res(equals_164_res));
  Equals equals_165 (.A(buscontrol_2_out_6), .B(8'h39), .res(equals_165_res));
  Equals equals_166 (.A(buscontrol_2_out_6), .B(8'h3a), .res(equals_166_res));
  Equals equals_167 (.A(buscontrol_2_out_6), .B(8'h3b), .res(equals_167_res));
  Equals equals_168 (.A(buscontrol_2_out_6), .B(8'h3c), .res(equals_168_res));
  Equals equals_169 (.A(buscontrol_2_out_6), .B(8'h3d), .res(equals_169_res));
  Equals equals_170 (.A(buscontrol_2_out_6), .B(8'h3e), .res(equals_170_res));
  Equals equals_171 (.A(buscontrol_2_out_6), .B(8'h3f), .res(equals_171_res));
  NCtoTF nctotf_119 (.A(equals_171_res), .res(nctotf_119_res));
  Multiplexer #(.width(8)) multiplexer_4 (
    .in0({controlled_buffer_3_out_2, controlled_buffer_3_out}), .in1(buscontrol_2_out_7),
    .out(multiplexer_4_out), .sel(equals_111_res));
  Multiplexer #(.width(8)) multiplexer_5 (
    .in0(controlled_buffer_39_out), .in1(buscontrol_2_out_8), .out(multiplexer_5_out), .sel(equals_111_res));
  or or_8 (or_8_out, equals_116_res, equals_115_res);
  or or_9 (or_9_out, or_8_out, equals_113_res);
  Multiplexer #(.width(8)) multiplexer_6 (
    .in0({controlled_buffer_3_out_2, controlled_buffer_3_out}), .in1(buscontrol_2_out_7),
    .out(multiplexer_6_out), .sel(or_8_out));
  Multiplexer #(.width(8)) multiplexer_7 (
    .in0(controlled_buffer_39_out), .in1(buscontrol_2_out_8), .out(multiplexer_7_out), .sel(or_9_out));
  or or_10 (or_10_out, equals_120_res, equals_118_res);
  Multiplexer #(.width(8)) multiplexer_8 (
    .in0(buscontrol_2_out_8), .in1(buscontrol_2_out_7), .out(multiplexer_8_out), .sel(or_10_out));
  assign xor_2_out = nctotf_111_res ^ {8{1'b1}};  // XOR_Gate xor_2, 8 bits wide
  Adder #(.width(16)) adder_1 (
    .a({buscontrol_2_out_7, buscontrol_2_out_8}), .b(counter_1_q), .out(adder_1_out));  // open: cin, cout
  Adder #(.width(16)) adder_2 (
    .a({buscontrol_2_out_7, buscontrol_2_out_8}), .b(counter_1_q), .out(adder_2_out));  // open: cin, cout
  or or_11 (or_11_out, equals_109_res, equals_111_res, equals_110_res);
  assign controlled_buffer_77_out = equals_110_res ? controlled_buffer_107_out[0] : 1'bz;  // Controlled_Buffer controlled_buffer_77
  AddMod addmod_1 (
    .A(multiplexer_4_out), .B(multiplexer_5_out), .CarryIN(controlled_buffer_77_out),
    .CarryOUT(addmod_1_carryout), .Negative(addmod_1_negative), .HalfCarryOUT(addmod_1_halfcarryout),
    .isaZero(addmod_1_isazero), .Result(addmod_1_result), .SignCarry(addmod_1_signcarry));
  smallOR smallor_2 (.in_1(equals_114_res), .in_2(equals_115_res), .out_3(smallor_2_out_3));
  assign controlled_buffer_78_out = smallor_2_out_3 ? controlled_buffer_107_out[0] : 1'bz;  // Controlled_Buffer controlled_buffer_78
  SubMod submod_1 (
    .A(multiplexer_6_out), .B(multiplexer_7_out), .CarryIN(controlled_buffer_78_out),
    .CarryOUT(submod_1_carryout), .Negative(submod_1_negative), .HalfCarryOUT(submod_1_halfcarryout),
    .isaZero(submod_1_isazero), .Result(submod_1_result), .SignCarry(submod_1_signcarry));
  Adder adder_3 (.a(8'h1), .b(xor_2_out), .out(adder_3_out));  // open: cin, cout
  Multiplexer #(.width(8)) multiplexer_9 (
    .in0({8{1'b0}}), .in1({8{1'b1}}), .out(multiplexer_9_out), .sel(equals_128_res));
  isZero iszero_1 (.in_1({controlled_buffer_3_out_2, controlled_buffer_3_out}), .out_2(iszero_1_out_2));
  or or_12 (or_12_out, equals_151_res, equals_152_res);
  or or_13 (or_13_out, equals_153_res, equals_154_res);
  or or_14 (or_14_out, equals_156_res, equals_157_res);
  RAM #(.addrWidth(16)) ram_1 (
    .addr(register_34_q), .we(equals_159_res), .oe(1'b1), .clk(controlled_buffer_1_out),
    .din({controlled_buffer_3_out_2, controlled_buffer_3_out}), .dout(ram_1_dout));
  and and_1 (and_1_out[0], or_25_out, controlled_buffer_107_out[0]);
  or or_15 (or_15_out, equals_168_res, equals_169_res);
  Decoder #(.select(3)) decoder_1 (
    .out0(decoder_1_out0), .out1(decoder_1_out1), .out2(decoder_1_out2), .out3(decoder_1_out3),
    .out4(decoder_1_out4), .out5(decoder_1_out5), .out6(decoder_1_out6), .out7(decoder_1_out7),
    .sel(controlled_buffer_3_out), .en(or_15_out));
  xor xor_3 (xor_3_out, addmod_1_negative, addmod_1_signcarry);
  assign controlled_buffer_79_out = or_11_out ? addmod_1_negative : 1'bz;  // Controlled_Buffer controlled_buffer_79
  assign controlled_buffer_80_out = or_11_out ? addmod_1_isazero : 1'bz;  // Controlled_Buffer controlled_buffer_80
  or or_16 (or_16_out, equals_112_res, equals_113_res, equals_114_res, equals_115_res, equals_116_res);
  or or_17 (or_17_out, equals_117_res, equals_118_res);
  or or_18 (or_18_out, equals_119_res, equals_120_res);
  or or_19 (or_19_out, equals_117_res, equals_118_res, equals_119_res, equals_120_res, equals_121_res, equals_122_res);
  isZero iszero_2 (.in_1(adder_3_out), .out_2(iszero_2_out_2));
  or or_20 (or_20_out, equals_127_res, equals_128_res);
  assign controlled_buffer_80_out = equals_127_res ? iszero_1_out_2 : 1'bz;  // Controlled_Buffer controlled_buffer_81
  assign controlled_buffer_79_out = equals_127_res ? controlled_buffer_3_out_2[4] : 1'bz;  // Controlled_Buffer controlled_buffer_82
  or or_21 (or_21_out, equals_129_res, equals_130_res);
  or or_22 (or_22_out, equals_131_res[0], equals_131_res[1], equals_131_res[2], equals_131_res[3], equals_131_res[4], equals_131_res[5], equals_131_res[6], equals_131_res[7], equals_131_res[8], equals_131_res[9], equals_131_res[10], equals_131_res[11], equals_131_res[12], equals_131_res[13], equals_131_res[14], equals_131_res[15], equals_131_res[16], equals_131_res[17], equals_131_res[18], equals_131_res[19]);
  and and_2 (and_2_out[7], or_25_out, controlled_buffer_107_out[0]);
  Register #(.width(1)) register_36 (
    .D(nctotf_120_res), .en(nctotf_121_res), .clk(controlled_buffer_1_out), .Q(controlled_buffer_107_out[7]),
    .clr(Reset_pin));
  NCtoTF nctotf_120 (.A(undriven_3), .res(nctotf_120_res));
  NCtoTF nctotf_121 (.A(tftonc_1_res), .res(nctotf_121_res));
  assign controlled_buffer_83_out = or_11_out ? xor_3_out : 1'bz;  // Controlled_Buffer controlled_buffer_83
  assign controlled_buffer_84_out = or_11_out ? addmod_1_signcarry : 1'bz;  // Controlled_Buffer controlled_buffer_84
  assign controlled_buffer_85_out = or_11_out ? addmod_1_halfcarryout : 1'bz;  // Controlled_Buffer controlled_buffer_85
  assign controlled_buffer_86_out = or_11_out ? addmod_1_carryout : 1'bz;  // Controlled_Buffer controlled_buffer_86
  xor xor_4 (xor_4_out, submod_1_negative, submod_1_signcarry);
  assign and_3_out = buscontrol_2_out_7 & multiplexer_8_out;  // AND_Gate and_3, 8 bits wide
  assign or_23_out = buscontrol_2_out_7 | multiplexer_8_out;  // OR_Gate or_23, 8 bits wide
  assign xor_5_out = buscontrol_2_out_7 ^ multiplexer_8_out;  // XOR_Gate xor_5, 8 bits wide
  Multiplexer #(.width(8)) multiplexer_10 (.in0(8'h1), .in1({8{1'b1}}), .out(multiplexer_10_out), .sel(equals_124_res));
  Stack stack_1 (
    .clock(controlled_buffer_1_out), .enable(or_14_out), .save_read(equals_156_res),
    .input_value({undriven_2, controlled_buffer_3_out_2, controlled_buffer_3_out}), .out_6(stack_1_out_6));  // open: on_edge
  Multiplexer #(.width(8)) multiplexer_11 (
    .in0({controlled_buffer_3_out_2[3:0], controlled_buffer_3_out, and_1_out[0]}),
    .in1({and_2_out[7], controlled_buffer_3_out_2, controlled_buffer_3_out[2:1]}), .out(multiplexer_11_out),
    .sel(equals_162_res));
  Multiplexer multiplexer_12 (
    .in0(controlled_buffer_3_out_2[4]), .in1(controlled_buffer_3_out[0]), .out(multiplexer_12_out),
    .sel(equals_162_res));
  Register #(.width(1)) register_37 (
    .D(nctotf_122_res), .en(nctotf_123_res), .clk(controlled_buffer_1_out), .Q(controlled_buffer_107_out[6]),
    .clr(Reset_pin));
  NCtoTF nctotf_122 (.A(undriven_4), .res(nctotf_122_res));
  NCtoTF nctotf_123 (.A(tftonc_2_res), .res(nctotf_123_res));
  assign controlled_buffer_87_out = or_18_out ? and_3_out : 8'bz;  // Controlled_Buffer controlled_buffer_87
  assign controlled_buffer_87_out = or_17_out ? or_23_out : 8'bz;  // Controlled_Buffer controlled_buffer_88
  Subtractor #(.width(7)) subtractor_1 (
    .a({7{1'b1}}), .b(buscontrol_2_out_7[14:8]), .out(subtractor_1_out[6:0]), .bout(subtractor_1_bout));  // open: bin
  Subtractor #(.width(1)) subtractor_2 (
    .a(1'b1), .b(buscontrol_2_out_7[15]), .out(subtractor_1_out[7]), .bin(subtractor_1_bout),
    .bout(subtractor_2_bout));
  or or_24 (or_24_out, equals_123_res, equals_124_res);
  Adder adder_4 (
    .a({controlled_buffer_3_out_2, controlled_buffer_3_out}), .b(multiplexer_10_out), .out(adder_4_out),
    .cout(adder_4_cout));  // open: cin
  isZero iszero_3 (.in_1(adder_4_out), .out_2(iszero_3_out_2));
  isZero iszero_4 (.in_1({controlled_buffer_3_out_2, controlled_buffer_3_out}), .out_2(iszero_4_out_2));
  or or_25 (or_25_out, equals_163_res, equals_164_res);
  assign controlled_buffer_107_out[7] = decoder_1_out0 ? equals_169_res : 1'bz;  // Controlled_Buffer controlled_buffer_89
  Register #(.width(1)) register_38 (
    .D(nctotf_124_res), .en(nctotf_125_res), .clk(controlled_buffer_1_out), .Q(controlled_buffer_107_out[5]),
    .clr(Reset_pin));
  NCtoTF nctotf_124 (.A(controlled_buffer_85_out), .res(nctotf_124_res));
  NCtoTF nctotf_125 (.A(tftonc_3_res), .res(nctotf_125_res));
  assign controlled_buffer_85_out = controlled_buffer_107_out[0] ? submod_1_halfcarryout : 1'bz;  // Controlled_Buffer controlled_buffer_90
  assign controlled_buffer_83_out = controlled_buffer_107_out[0] ? xor_4_out : 1'bz;  // Controlled_Buffer controlled_buffer_91
  assign controlled_buffer_84_out = controlled_buffer_107_out[0] ? submod_1_signcarry : 1'bz;  // Controlled_Buffer controlled_buffer_92
  assign controlled_buffer_79_out = controlled_buffer_107_out[0] ? submod_1_negative : 1'bz;  // Controlled_Buffer controlled_buffer_93
  assign controlled_buffer_80_out = controlled_buffer_107_out[0] ? submod_1_isazero : 1'bz;  // Controlled_Buffer controlled_buffer_94
  assign controlled_buffer_86_out = controlled_buffer_107_out[0] ? submod_1_carryout : 1'bz;  // Controlled_Buffer controlled_buffer_95
  assign controlled_buffer_87_out = equals_121_res ? xor_5_out : 8'bz;  // Controlled_Buffer controlled_buffer_96
  assign controlled_buffer_87_out = equals_122_res ? subtractor_1_out : 8'bz;  // Controlled_Buffer controlled_buffer_97
  isZero iszero_5 (.in_1(controlled_buffer_87_out), .out_2(iszero_5_out_2));
  assign controlled_buffer_80_out = or_24_out ? iszero_3_out_2 : 1'bz;  // Controlled_Buffer controlled_buffer_98
  assign controlled_buffer_79_out = or_24_out ? adder_4_out[7] : 1'bz;  // Controlled_Buffer controlled_buffer_99
  assign controlled_buffer_84_out = or_24_out ? adder_4_cout : 1'bz;  // Controlled_Buffer controlled_buffer_100
  assign controlled_buffer_80_out = equals_125_res ? iszero_4_out_2 : 1'bz;  // Controlled_Buffer controlled_buffer_101
  assign controlled_buffer_79_out = equals_125_res ? controlled_buffer_3_out_2[4] : 1'bz;  // Controlled_Buffer controlled_buffer_102
  assign controlled_buffer_79_out = equals_126_res ? adder_3_out[0] : 1'bz;  // Controlled_Buffer controlled_buffer_103
  assign controlled_buffer_80_out = equals_126_res ? iszero_2_out_2 : 1'bz;  // Controlled_Buffer controlled_buffer_104
  and and_4 (not_2_out[10], controlled_buffer_107_out[2], controlled_buffer_107_out[3]);
  or or_26 (not_2_out[11], controlled_buffer_107_out[2], controlled_buffer_107_out[3]);
  isZero iszero_6 (
    .in_1({{2{controlled_buffer_3_out_2[4]}}, controlled_buffer_3_out_2[3:0], controlled_buffer_3_out[2:1]}),
    .out_2(iszero_6_out_2));
  or or_27 (or_27_out, equals_161_res, equals_162_res, equals_163_res, equals_164_res);
  assign controlled_buffer_107_out[6] = decoder_1_out1 ? equals_169_res : 1'bz;  // Controlled_Buffer controlled_buffer_105
  assign controlled_buffer_107_out[5] = decoder_1_out2 ? equals_169_res : 1'bz;  // Controlled_Buffer controlled_buffer_106
  assign controlled_buffer_107_out[4] = decoder_1_out3 ? equals_169_res : 1'bz;  // Controlled_Buffer controlled_buffer_107
  assign controlled_buffer_107_out[3] = decoder_1_out4 ? equals_169_res : 1'bz;  // Controlled_Buffer controlled_buffer_108
  LedBar ledbar_1 (
    .led0(controlled_buffer_107_out[7]), .led1(controlled_buffer_107_out[6]),
    .led2(controlled_buffer_107_out[5]), .led3(controlled_buffer_107_out[4]),
    .led4(controlled_buffer_107_out[3]), .led5(controlled_buffer_107_out[2]),
    .led6(controlled_buffer_107_out[1]), .led7(controlled_buffer_107_out[0]));
  NCtoTF nctotf_126 (.A(controlled_buffer_83_out), .res(nctotf_126_res));
  NCtoTF nctotf_127 (.A(tftonc_4_res), .res(nctotf_127_res));
  assign controlled_buffer_80_out = or_19_out ? iszero_5_out_2 : 1'bz;  // Controlled_Buffer controlled_buffer_109
  assign controlled_buffer_84_out = equals_122_res ? subtractor_1_bout : 1'bz;  // Controlled_Buffer controlled_buffer_110
  assign controlled_buffer_79_out = or_19_out ? controlled_buffer_87_out[7] : 1'bz;  // Controlled_Buffer controlled_buffer_111
  assign controlled_buffer_86_out = equals_122_res ? subtractor_2_bout : 1'bz;  // Controlled_Buffer controlled_buffer_112
  not not_2 (not_2_out[0], not_2_out[1]);
  not not_3 (not_2_out[3], controlled_buffer_107_out[0]);
  not not_4 (not_2_out[5], controlled_buffer_107_out[1]);
  not not_5 (not_2_out[6], controlled_buffer_107_out[0]);
  not not_6 (not_2_out[9], controlled_buffer_107_out[2]);
  not not_7 (not_2_out[13], controlled_buffer_107_out[5]);
  not not_8 (not_2_out[15], controlled_buffer_107_out[6]);
  not not_9 (not_2_out[17], controlled_buffer_107_out[3]);
  not not_10 (not_2_out[19], controlled_buffer_107_out[7]);
  assign controlled_buffer_80_out = equals_160_res ? iszero_6_out_2 : 1'bz;  // Controlled_Buffer controlled_buffer_113
  assign controlled_buffer_86_out = equals_160_res ? controlled_buffer_3_out[0] : 1'bz;  // Controlled_Buffer controlled_buffer_114
  Controlled_Buffer controlled_buffer_115 (.in(iszero_7_out_2), .en(or_27_out));  // open: out
  isZero iszero_7 (.in_1(multiplexer_11_out), .out_2(iszero_7_out_2));
  Controlled_Buffer controlled_buffer_116 (.in(multiplexer_12_out), .out(controlled_buffer_86_out));  // open: en
  TFtoNC tftonc_1 (.A(decoder_1_out0), .Res(tftonc_1_res));
  assign controlled_buffer_107_out[2] = decoder_1_out5 ? equals_169_res : 1'bz;  // Controlled_Buffer controlled_buffer_117
  assign controlled_buffer_107_out[1] = decoder_1_out6 ? equals_169_res : 1'bz;  // Controlled_Buffer controlled_buffer_118
  assign controlled_buffer_107_out[0] = decoder_1_out7 ? equals_169_res : 1'bz;  // Controlled_Buffer controlled_buffer_119
  Register #(.width(1)) register_39 (
    .D(nctotf_126_res), .en(nctotf_127_res), .clk(controlled_buffer_1_out), .Q(controlled_buffer_107_out[4]),
    .clr(Reset_pin));
  TFtoNC tftonc_2 (.A(decoder_1_out1), .Res(tftonc_2_res));
  Register #(.width(1)) register_40 (
    .D(nctotf_128_res), .en(nctotf_129_res), .clk(controlled_buffer_1_out), .Q(controlled_buffer_107_out[3]),
    .clr(Reset_pin));
  NCtoTF nctotf_128 (.A(controlled_buffer_84_out), .res(nctotf_128_res));
  NCtoTF nctotf_129 (.A(tftonc_9_res), .res(nctotf_129_res));
  TFtoNC tftonc_3 (.A(or_11_out), .Res(tftonc_3_res));
  TFtoNC tftonc_4 (.A(or_11_out), .Res(tftonc_4_res));
  TFtoNC tftonc_5 (.A(or_16_out), .Res(tftonc_3_res));
  TFtoNC tftonc_6 (.A(or_16_out), .Res(tftonc_4_res));
  TFtoNC tftonc_7 (.A(decoder_1_out2), .Res(tftonc_3_res));
  TFtoNC tftonc_8 (.A(decoder_1_out3), .Res(tftonc_4_res));
  Register #(.width(1)) register_41 (
    .D(nctotf_130_res), .en(nctotf_131_res), .clk(controlled_buffer_1_out), .Q(controlled_buffer_107_out[2]),
    .clr(Reset_pin));
  NCtoTF nctotf_130 (.A(controlled_buffer_79_out), .res(nctotf_130_res));
  NCtoTF nctotf_131 (.A(tftonc_14_res), .res(nctotf_131_res));
  TFtoNC tftonc_9 (.A(or_11_out), .Res(tftonc_9_res));
  TFtoNC tftonc_10 (.A(or_16_out), .Res(tftonc_9_res));
  TFtoNC tftonc_11 (.A(or_19_out), .Res(tftonc_9_res));
  TFtoNC tftonc_12 (.A(or_24_out), .Res(tftonc_9_res));
  TFtoNC tftonc_13 (.A(decoder_1_out4), .Res(tftonc_9_res));
  Register #(.width(1)) register_42 (
    .D(nctotf_132_res), .en(nctotf_133_res), .clk(controlled_buffer_1_out), .Q(controlled_buffer_107_out[1]),
    .clr(Reset_pin));
  NCtoTF nctotf_132 (.A(controlled_buffer_80_out), .res(nctotf_132_res));
  NCtoTF nctotf_133 (.A(tftonc_22_res), .res(nctotf_133_res));
  TFtoNC tftonc_14 (.A(or_11_out), .Res(tftonc_14_res));
  TFtoNC tftonc_15 (.A(or_16_out), .Res(tftonc_14_res));
  TFtoNC tftonc_16 (.A(or_19_out), .Res(tftonc_14_res));
  TFtoNC tftonc_17 (.A(or_24_out), .Res(tftonc_14_res));
  TFtoNC tftonc_18 (.A(equals_125_res), .Res(tftonc_14_res));
  TFtoNC tftonc_19 (.A(equals_126_res), .Res(tftonc_14_res));
  TFtoNC tftonc_20 (.A(equals_127_res), .Res(tftonc_14_res));
  TFtoNC tftonc_21 (.A(decoder_1_out5), .Res(tftonc_14_res));
  NCtoTF nctotf_134 (.A(controlled_buffer_86_out), .res(nctotf_134_res));
  NCtoTF nctotf_135 (.A(tftonc_23_res), .res(nctotf_135_res));
  TFtoNC tftonc_22 (.A(or_11_out), .Res(tftonc_22_res));
  TFtoNC tftonc_23 (.A(or_11_out), .Res(tftonc_23_res));
  TFtoNC tftonc_24 (.A(or_16_out), .Res(tftonc_22_res));
  TFtoNC tftonc_25 (.A(or_16_out), .Res(tftonc_23_res));
  TFtoNC tftonc_26 (.A(or_19_out), .Res(tftonc_22_res));
  TFtoNC tftonc_27 (.A(equals_122_res), .Res(tftonc_23_res));
  TFtoNC tftonc_28 (.A(or_24_out), .Res(tftonc_22_res));
  TFtoNC tftonc_29 (.A(equals_125_res), .Res(tftonc_22_res));
  TFtoNC tftonc_30 (.A(equals_126_res), .Res(tftonc_22_res));
  TFtoNC tftonc_31 (.A(equals_127_res), .Res(tftonc_22_res));
  TFtoNC tftonc_32 (.A(equals_160_res), .Res(tftonc_22_res));
  TFtoNC tftonc_33 (.A(equals_160_res), .Res(tftonc_23_res));
  TFtoNC tftonc_34 (.A(or_27_out), .Res(tftonc_22_res));
  TFtoNC tftonc_35 (.A(or_27_out), .Res(tftonc_23_res));
  TFtoNC tftonc_36 (.A(decoder_1_out6), .Res(tftonc_22_res));
  TFtoNC tftonc_37 (.A(decoder_1_out7), .Res(tftonc_23_res));
  Register #(.width(1)) register_43 (
    .D(nctotf_134_res), .en(nctotf_135_res), .clk(controlled_buffer_1_out), .Q(controlled_buffer_107_out[0]),
    .clr(Reset_pin));
  assign controlled_buffer_120_out = equals_108_res ? {controlled_buffer_3_out_2, controlled_buffer_3_out} : 8'bz;  // Controlled_Buffer controlled_buffer_120
  assign controlled_buffer_121_out = equals_108_res ? buscontrol_2_out_7 : 8'bz;  // Controlled_Buffer controlled_buffer_121
  assign controlled_buffer_120_out = or_11_out ? addmod_1_result : 8'bz;  // Controlled_Buffer controlled_buffer_122
  assign controlled_buffer_121_out = or_11_out ? buscontrol_2_out_9 : 8'bz;  // Controlled_Buffer controlled_buffer_123
  assign controlled_buffer_120_out = or_16_out ? submod_1_result : 8'bz;  // Controlled_Buffer controlled_buffer_124
  assign controlled_buffer_121_out = or_16_out ? buscontrol_2_out_9 : 8'bz;  // Controlled_Buffer controlled_buffer_125
  assign controlled_buffer_120_out = or_19_out ? controlled_buffer_87_out : 8'bz;  // Controlled_Buffer controlled_buffer_126
  assign controlled_buffer_121_out = or_19_out ? buscontrol_2_out_9 : 8'bz;  // Controlled_Buffer controlled_buffer_127
  assign controlled_buffer_120_out = or_24_out ? adder_4_out : 8'bz;  // Controlled_Buffer controlled_buffer_128
  assign controlled_buffer_121_out = or_24_out ? buscontrol_2_out_9 : 8'bz;  // Controlled_Buffer controlled_buffer_129
  assign controlled_buffer_120_out = equals_125_res ? {controlled_buffer_3_out_2, controlled_buffer_3_out} : 8'bz;  // Controlled_Buffer controlled_buffer_130
  assign controlled_buffer_121_out = equals_125_res ? buscontrol_2_out_7 : 8'bz;  // Controlled_Buffer controlled_buffer_131
  assign controlled_buffer_120_out = equals_126_res ? adder_3_out : 8'bz;  // Controlled_Buffer controlled_buffer_132
  assign controlled_buffer_121_out = equals_126_res ? buscontrol_2_out_9 : 8'bz;  // Controlled_Buffer controlled_buffer_133
  assign controlled_buffer_120_out = or_20_out ? multiplexer_9_out : 8'bz;  // Controlled_Buffer controlled_buffer_134
  assign controlled_buffer_121_out = or_20_out ? buscontrol_2_out_7 : 8'bz;  // Controlled_Buffer controlled_buffer_135
  assign controlled_buffer_120_out = or_21_out ? {controlled_buffer_3_out_2, controlled_buffer_3_out} : 8'bz;  // Controlled_Buffer controlled_buffer_136
  assign controlled_buffer_121_out = or_21_out ? buscontrol_2_out_7 : 8'bz;  // Controlled_Buffer controlled_buffer_137
  assign controlled_buffer_120_out = or_22_out ? {controlled_buffer_3_out_2, controlled_buffer_3_out} : 8'bz;  // Controlled_Buffer controlled_buffer_138
  assign controlled_buffer_121_out = or_22_out ? buscontrol_2_out_7 : 8'bz;  // Controlled_Buffer controlled_buffer_139
  assign controlled_buffer_120_out = or_12_out ? {controlled_buffer_3_out_2, controlled_buffer_3_out} : 8'bz;  // Controlled_Buffer controlled_buffer_140
  assign controlled_buffer_121_out = or_12_out ? buscontrol_2_out_7 : 8'bz;  // Controlled_Buffer controlled_buffer_141
  assign controlled_buffer_120_out = or_13_out ? {controlled_buffer_3_out_2, controlled_buffer_3_out} : 8'bz;  // Controlled_Buffer controlled_buffer_142
  assign controlled_buffer_121_out = or_13_out ? buscontrol_2_out_7 : 8'bz;  // Controlled_Buffer controlled_buffer_143
  assign controlled_buffer_120_out = or_7_out[1] ? {controlled_buffer_3_out_2, controlled_buffer_3_out} : 8'bz;  // Controlled_Buffer controlled_buffer_144
  assign controlled_buffer_121_out = or_7_out[1] ? buscontrol_2_out_7 : 8'bz;  // Controlled_Buffer controlled_buffer_145
  assign controlled_buffer_120_out = equals_156_res ? {controlled_buffer_3_out_2, controlled_buffer_3_out} : 8'bz;  // Controlled_Buffer controlled_buffer_146
  assign controlled_buffer_121_out = equals_156_res ? buscontrol_2_out_7 : 8'bz;  // Controlled_Buffer controlled_buffer_147
  assign controlled_buffer_120_out = equals_157_res ? stack_1_out_6[7:0] : 8'bz;  // Controlled_Buffer controlled_buffer_148
  assign controlled_buffer_121_out = equals_157_res ? buscontrol_2_out_9 : 8'bz;  // Controlled_Buffer controlled_buffer_149
  assign controlled_buffer_120_out = equals_158_res ? ram_1_dout : 8'bz;  // Controlled_Buffer controlled_buffer_150
  assign controlled_buffer_121_out = equals_158_res ? buscontrol_2_out_9 : 8'bz;  // Controlled_Buffer controlled_buffer_151
  assign controlled_buffer_120_out = equals_159_res ? {controlled_buffer_3_out_2, controlled_buffer_3_out} : 8'bz;  // Controlled_Buffer controlled_buffer_152
  assign controlled_buffer_121_out = equals_159_res ? buscontrol_2_out_7 : 8'bz;  // Controlled_Buffer controlled_buffer_153
  assign controlled_buffer_120_out = equals_160_res ? {{2{controlled_buffer_3_out_2[4]}}, controlled_buffer_3_out_2[3:0], controlled_buffer_3_out[2:1]} : 8'bz;  // Controlled_Buffer controlled_buffer_154
  assign controlled_buffer_121_out = equals_160_res ? buscontrol_2_out_9 : 8'bz;  // Controlled_Buffer controlled_buffer_155
  assign controlled_buffer_120_out = or_27_out ? multiplexer_11_out : 8'bz;  // Controlled_Buffer controlled_buffer_156
  assign controlled_buffer_121_out = or_27_out ? buscontrol_2_out_9 : 8'bz;  // Controlled_Buffer controlled_buffer_157
  assign controlled_buffer_120_out = equals_165_res ? {controlled_buffer_3_out_2[0], controlled_buffer_3_out, controlled_buffer_3_out_2[4:1]} : 8'bz;  // Controlled_Buffer controlled_buffer_158
  assign controlled_buffer_121_out = equals_165_res ? buscontrol_2_out_9 : 8'bz;  // Controlled_Buffer controlled_buffer_159
  assign controlled_buffer_120_out = equals_166_res ? controlled_buffer_170_out : 8'bz;  // Controlled_Buffer controlled_buffer_160
  assign controlled_buffer_121_out = equals_166_res ? buscontrol_2_out_9 : 8'bz;  // Controlled_Buffer controlled_buffer_161
  assign controlled_buffer_120_out = equals_167_res ? {controlled_buffer_3_out_2, controlled_buffer_3_out} : 8'bz;  // Controlled_Buffer controlled_buffer_162
  assign controlled_buffer_121_out = equals_167_res ? buscontrol_2_out_7 : 8'bz;  // Controlled_Buffer controlled_buffer_163
  assign controlled_buffer_120_out = or_15_out ? {controlled_buffer_3_out_2, controlled_buffer_3_out} : 8'bz;  // Controlled_Buffer controlled_buffer_164
  assign controlled_buffer_121_out = or_15_out ? buscontrol_2_out_7 : 8'bz;  // Controlled_Buffer controlled_buffer_165
  assign controlled_buffer_120_out = equals_170_res ? {controlled_buffer_3_out_2, controlled_buffer_3_out} : 8'bz;  // Controlled_Buffer controlled_buffer_166
  assign controlled_buffer_121_out = equals_170_res ? buscontrol_2_out_7 : 8'bz;  // Controlled_Buffer controlled_buffer_167
  assign controlled_buffer_120_out = equals_171_res ? {controlled_buffer_3_out_2, controlled_buffer_3_out} : 8'bz;  // Controlled_Buffer controlled_buffer_168
  assign controlled_buffer_121_out = equals_171_res ? buscontrol_2_out_7 : 8'bz;  // Controlled_Buffer controlled_buffer_169
  assign and_5_out = equals_131_res & {not_2_out[19], controlled_buffer_107_out[7], not_2_out[17], controlled_buffer_107_out[3], not_2_out[15], controlled_buffer_107_out[6], not_2_out[13], controlled_buffer_107_out[5], not_2_out[11:9], controlled_buffer_107_out[2], controlled_buffer_107_out[0], not_2_out[6:5], controlled_buffer_107_out[1], not_2_out[3], controlled_buffer_107_out[0], not_2_out[1:0]};  // AND_Gate and_5, 20 bits wide
  or or_28 (or_28_out, and_5_out[0], and_5_out[1], and_5_out[2], and_5_out[3], and_5_out[4], and_5_out[5], and_5_out[6], and_5_out[7], and_5_out[8], and_5_out[9], and_5_out[10], and_5_out[11], and_5_out[12], and_5_out[13], and_5_out[14], and_5_out[15], and_5_out[16], and_5_out[17], and_5_out[18], and_5_out[19], or_12_out, or_13_out, or_7_out[1]);
  or or_29 (or_29_out, or_13_out, or_7_out[1]);
  assign controlled_buffer_170_out = equals_166_res ? IN_OUT : 8'bz;  // Controlled_Buffer controlled_buffer_170
  assign out_3 = equals_167_res ? {controlled_buffer_3_out_2, controlled_buffer_3_out} : 8'bz;  // Controlled_Buffer controlled_buffer_171
  Stack stack_2 (
    .clock(controlled_buffer_1_out), .enable(or_29_out), .save_read(or_13_out), .input_value(counter_1_q),
    .out_6(stack_2_out_6));  // open: on_edge
  LED led_1 (.in(equals_166_res));
  LED led_2 (.in(equals_167_res));
  // Probe on stack_2_out_6
  Adder #(.width(16)) adder_5 (.a(stack_2_out_6), .b(16'h1), .out(adder_5_out));  // open: cin, cout
  // RGB_Video #(.cursor("No Cursor"), .height(64), .scale(4), .width(64)) rgb_video_1: pin names not known; wires that end beside it: Reset_pin, equals_167_res, 1'b1, X[5:0], Y[5:0], RGB

  // Notes on the sheet:
  //   LD/ST REGS
  //   WDR REG
  //   contents of Main_Programm (hex, n*v repeats v):
  //   3 3f 0 3 3 4 0 4 4 1b 3 2 11 2 0 0 16 0 d 0 1b 0 0 0 1 1d 4 1d 1 1e 4 1e 1 1f 4 1f 3b 0 0 0 f 1b 0
  //   1b 16 0 2 0 2c 0 0 0 3b 0 0 0 f 1c 0 1c 3 0 0 1b 3 0 0 1d 3 0 0 1e 3 0 0 1f 16 0 2 0 2c
  //   OPCODE
  //   DATA BUS
  //   ADDR1
  //   ADDR2
  //   RESADDR
  //   To I Flag
  //   CPU
  //   AU
  //   LU
  //   TST
  //   NEG
  //   RET
  //   LD/ST
  //   ASR
  //   SWAP
  //   IN/OUT
  //   WDR
  //   HALT
  //   MAIN PROGRAMM BUS
  //   RESET LINE
  //   INC/DEC
  //   CLR/SER
  //   SJR/SJRW
  //   JMP CMD
  //   RJMP/JMP
  //   RCALL/CALL
  //   PUSH/POP
  //   LSL/LSR
  //   ROL/ROR
  //   BSET/BCLR
  //   SOBOL
  //   REV-5
  //   Версия от 01.06.2025 14:35
  //   Автор: Шамрин А. Н.
  //   I
  //   T
  //   SREG
  //   I T H S V N Z C
  //   H
  //   S
  //   V
  //   N
  //   Z
  //   C
endmodule

module Stack (
  input  [15:0] input_value,
  input  clock,
  input  enable,
  input  save_read,
  output on_edge,
  output [15:0] out_6
);

  wire comparator_1_eq, comparator_2_eq, xor_1_out;
  wire [15:0] counter_1_q;

  xor xor_1 (xor_1_out, clock, enable);
  Counter #(.max('hffff), .width(16)) counter_1 (
    .count(enable), .Q(counter_1_q), .up(save_read), .clk(xor_1_out));  // open: load, D, carry, clr
  or or_1 (on_edge, comparator_1_eq, comparator_2_eq);
  Comparator #(.width(16)) comparator_1 (.a({16{1'b1}}), .b(counter_1_q), .eq(comparator_1_eq));  // open: gt, lt
  Comparator #(.width(16)) comparator_2 (.a({16{1'b0}}), .b(counter_1_q), .eq(comparator_2_eq));  // open: gt, lt
  RAM #(.addrWidth(16), .asyncread("true"), .dataWidth(16), .trigger("falling")) stack_memory (
    .addr(counter_1_q), .we(save_read), .oe(1'b1), .clk(xor_1_out), .din(input_value), .dout(out_6));

  // Notes on the sheet:
  //   Push - 1
  //   Pop - 0
endmodule

module Equals (
  input  [7:0] A,
  input  [7:0] B,
  output res
);

  Comparator #(.mode("unsigned")) comparator_1 (.a(A), .b(B), .eq(res));  // open: gt, lt
endmodule

module smallOR (
  input  in_1,
  input  in_2,
  output out_3
);

  or or_1 (out_3, in_1, in_2);
endmodule

module busControl (
  input  [7:0] in_1,
  input  [7:0] in_2,
  input  [7:0] in_3,
  input  [7:0] in_4,
  input  in_5,
  output [7:0] out_6,
  output [7:0] out_7,
  output [7:0] out_8,
  output [7:0] out_9
);

  assign out_9 = in_5 ? in_4 : 8'bz;  // Controlled_Buffer controlled_buffer_1
  assign out_6 = in_5 ? in_1 : 8'bz;  // Controlled_Buffer controlled_buffer_2
  assign out_7 = in_5 ? in_2 : 8'bz;  // Controlled_Buffer controlled_buffer_3
  assign out_8 = in_5 ? in_3 : 8'bz;  // Controlled_Buffer controlled_buffer_4
endmodule

module increment (
  input  [7:0] A,
  output [7:0] B
);

  Adder adder_1 (.a(8'h1), .b(A), .out(B));  // open: cin, cout
endmodule

module AddMod (
  input  CarryIN,
  input  [7:0] A,
  input  [7:0] B,
  output Negative,
  output isaZero,
  output [7:0] Result,
  output CarryOUT,
  output HalfCarryOUT,
  output SignCarry
);

  Adder #(.width(3)) adder_1 (.a(A[2:0]), .b(B[2:0]), .out(Result[2:0]), .cin(CarryIN), .cout(HalfCarryOUT));
  Adder #(.width(4)) adder_2 (.a(A[6:3]), .b(B[6:3]), .out(Result[6:3]), .cin(HalfCarryOUT), .cout(SignCarry));
  Adder #(.width(1)) adder_3 (.a(A[7]), .b(B[7]), .out(Negative), .cin(SignCarry), .cout(CarryOUT));
  isZero iszero_1 (.in_1({Negative, Result[6:0]}), .out_2(isaZero));

  assign Result[7] = Negative;
endmodule

module SubMod (
  input  CarryIN,
  input  [7:0] A,
  input  [7:0] B,
  output Negative,
  output isaZero,
  output [7:0] Result,
  output CarryOUT,
  output HalfCarryOUT,
  output SignCarry
);

  Subtractor #(.width(3)) subtractor_1 (.a(A[2:0]), .b(B[2:0]), .out(Result[2:0]), .bin(CarryIN), .bout(HalfCarryOUT));
  Subtractor #(.width(4)) subtractor_2 (
    .a(A[6:3]), .b(B[6:3]), .out(Result[6:3]), .bin(HalfCarryOUT), .bout(SignCarry));
  Subtractor #(.width(1)) subtractor_3 (.a(A[7]), .b(B[7]), .out(Negative), .bin(SignCarry), .bout(CarryOUT));
  isZero iszero_1 (.in_1({Negative, Result[6:0]}), .out_2(isaZero));

  assign Result[7] = Negative;
endmodule

module TFtoNC (
  input  A,
  output Res
);

  assign Res = A ? A : 1'bz;  // Controlled_Buffer controlled_buffer_1
endmodule

module NCtoTF (
  input  A,
  output res
);


  assign res = A;
endmodule

module isZero (
  input  [7:0] in_1,
  output out_2
);

  wire or_1_out;

  or or_1 (or_1_out, in_1[0], in_1[1], in_1[2], in_1[3], in_1[4], in_1[5], in_1[6], in_1[7]);
  not not_1 (out_2, or_1_out);
endmodule
